// Logisim project PROJECT (1).circ as structural Verilog
module byte_reigister_in_RAM (
  input  [2:0] _3A_INPUT,
  input  BIT,
  input  BIT_2,
  input  BIT_3,
  input  BIT_4,
  input  BIT_5,
  input  BIT_6,
  input  BIT_7,
  input  BIT_8,
  output [7:0] OUTPUT
);

  wire and_1_out;

  and and_1 (and_1_out, _3A_INPUT[0], _3A_INPUT[1], _3A_INPUT[2]);
  D_Flip_Flop d_ff_1 (.clk(and_1_out), .D(BIT), .Q(OUTPUT[7]));  // open: Qn, preset, en, reset
  D_Flip_Flop d_ff_2 (.clk(and_1_out), .D(BIT_2), .Q(OUTPUT[6]));  // open: Qn, preset, en, reset
  D_Flip_Flop d_ff_3 (.clk(and_1_out), .D(BIT_3), .Q(OUTPUT[5]));  // open: Qn, preset, en, reset
  D_Flip_Flop d_ff_4 (.clk(and_1_out), .D(BIT_4), .Q(OUTPUT[4]));  // open: Qn, preset, en, reset
  D_Flip_Flop d_ff_5 (.clk(and_1_out), .D(BIT_5), .Q(OUTPUT[3]));  // open: Qn, preset, en, reset
  D_Flip_Flop d_ff_6 (.clk(and_1_out), .D(BIT_6), .Q(OUTPUT[2]));  // open: Qn, preset, en, reset
  D_Flip_Flop d_ff_7 (.clk(and_1_out), .D(BIT_7), .Q(OUTPUT[1]));  // open: Qn, preset, en, reset
  D_Flip_Flop d_ff_8 (.clk(and_1_out), .D(BIT_8), .Q(OUTPUT[0]));  // open: Qn, preset, en, reset
endmodule

module RAM (
  input  in_1,
  input  [3:0] ADDR,
  input  in_3,
  input  INPUT_1,
  input  INPUT_2,
  input  [7:0] INPUT,
  output [7:0] OUTPUT
);

  wire decoder_1_out0, decoder_1_out1, decoder_1_out2, decoder_1_out3, decoder_1_out4, decoder_1_out5,
       decoder_1_out6, decoder_1_out7, decoder_1_out8, decoder_1_out9, decoder_1_out10, decoder_1_out11,
       decoder_1_out12, decoder_1_out13, decoder_1_out14, decoder_1_out15;
  wire [2:1] or_2_out;
  wire [2:2] or_3_out, or_4_out, or_5_out, or_6_out, or_7_out, or_8_out, or_9_out, or_10_out, or_11_out,
       or_12_out, or_13_out, or_14_out, or_15_out, or_16_out, or_17_out;
  wire [7:0] _14_output, _15_output, byte1_1_output, byte2_1_output, byte3_1_output, byte4_1_output,
       byte5_1_output, byte6_1_output, byte7_1_output, byte8_1_output, byte9_1_output, byte10_1_output,
       byte11_1_output, byte12_1_output, byte13_1_output, byte_0_1_output;

  Decoder #(.select(4)) decoder_1 (
    .out0(decoder_1_out0), .out1(decoder_1_out1), .out2(decoder_1_out2), .out3(decoder_1_out3),
    .out4(decoder_1_out4), .out5(decoder_1_out5), .out6(decoder_1_out6), .out7(decoder_1_out7),
    .out8(decoder_1_out8), .out9(decoder_1_out9), .out10(decoder_1_out10), .out11(decoder_1_out11),
    .out12(decoder_1_out12), .out13(decoder_1_out13), .out14(decoder_1_out14), .out15(decoder_1_out15),
    .sel(ADDR));  // open: en
  or or_1 (or_2_out[1], INPUT_2, in_3);
  buf or_2 (or_2_out[2], decoder_1_out15);  // OR_Gate
  buf or_3 (or_3_out[2], decoder_1_out14);  // OR_Gate
  or or_4 (or_4_out[2], decoder_1_out13, in_1);
  or or_5 (or_5_out[2], decoder_1_out12, in_1);
  or or_6 (or_6_out[2], decoder_1_out11, in_1);
  or or_7 (or_7_out[2], decoder_1_out10, in_1);
  or or_8 (or_8_out[2], decoder_1_out9, in_1);
  or or_9 (or_9_out[2], decoder_1_out8, in_1);
  or or_10 (or_10_out[2], decoder_1_out7, in_1);
  or or_11 (or_11_out[2], decoder_1_out6, in_1);
  or or_12 (or_12_out[2], decoder_1_out5, in_1);
  or or_13 (or_13_out[2], decoder_1_out4, in_1);
  or or_14 (or_14_out[2], decoder_1_out3, in_1);
  or or_15 (or_15_out[2], decoder_1_out2, in_1);
  or or_16 (or_16_out[2], decoder_1_out1, in_1);
  or or_17 (or_17_out[2], decoder_1_out0, in_1);
  byte_reigister_in_RAM _15 (
    .BIT(INPUT[7]), .BIT_2(INPUT[6]), .BIT_3(INPUT[5]), .BIT_4(INPUT[4]), .BIT_5(INPUT[3]), .BIT_6(INPUT[2]),
    .BIT_7(INPUT[1]), .BIT_8(INPUT[0]), ._3A_INPUT({or_2_out, INPUT_1}), .OUTPUT(_15_output));
  byte_reigister_in_RAM _14 (
    .BIT(INPUT[7]), .BIT_2(INPUT[6]), .BIT_3(INPUT[5]), .BIT_4(INPUT[4]), .BIT_5(INPUT[3]), .BIT_6(INPUT[2]),
    .BIT_7(INPUT[1]), .BIT_8(INPUT[0]), ._3A_INPUT({or_3_out[2], or_2_out[1], INPUT_1}), .OUTPUT(_14_output));
  byte13 byte13_1 (
    ._3A_INPUT({or_4_out[2], or_2_out[1], INPUT_1}), .in_2(INPUT[7]), .in_3(INPUT[6]), .in_4(INPUT[5]),
    .in_5(INPUT[4]), .in_6(INPUT[3]), .in_7(INPUT[2]), .in_8(INPUT[1]), .in_9(INPUT[0]),
    .OUTPUT(byte13_1_output));
  byte12 byte12_1 (
    ._3A_INPUT({or_5_out[2], or_2_out[1], INPUT_1}), .in_2(INPUT[7]), .in_3(INPUT[6]), .in_4(INPUT[5]),
    .in_5(INPUT[4]), .in_6(INPUT[3]), .in_7(INPUT[2]), .in_8(INPUT[1]), .in_9(INPUT[0]),
    .OUTPUT(byte12_1_output));
  byte11 byte11_1 (
    ._3A_INPUT({or_6_out[2], or_2_out[1], INPUT_1}), .in_2(INPUT[7]), .in_3(INPUT[6]), .in_4(INPUT[5]),
    .in_5(INPUT[4]), .in_6(INPUT[3]), .in_7(INPUT[2]), .in_8(INPUT[1]), .in_9(INPUT[0]),
    .OUTPUT(byte11_1_output));
  byte10 byte10_1 (
    ._3A_INPUT({or_7_out[2], or_2_out[1], INPUT_1}), .in_2(INPUT[7]), .in_3(INPUT[6]), .in_4(INPUT[5]),
    .in_5(INPUT[4]), .in_6(INPUT[3]), .in_7(INPUT[2]), .in_8(INPUT[1]), .in_9(INPUT[0]),
    .OUTPUT(byte10_1_output));
  byte8 byte8_1 (
    ._3A_INPUT({or_9_out[2], or_2_out[1], INPUT_1}), .in_2(INPUT[7]), .in_3(INPUT[6]), .in_4(INPUT[5]),
    .in_5(INPUT[4]), .in_6(INPUT[3]), .in_7(INPUT[2]), .in_8(INPUT[1]), .in_9(INPUT[0]),
    .OUTPUT(byte8_1_output));
  byte7 byte7_1 (
    ._3A_INPUT({or_10_out[2], or_2_out[1], INPUT_1}), .in_2(INPUT[7]), .in_3(INPUT[6]), .in_4(INPUT[5]),
    .in_5(INPUT[4]), .in_6(INPUT[3]), .in_7(INPUT[2]), .in_8(INPUT[1]), .in_9(INPUT[0]),
    .OUTPUT(byte7_1_output));
  byte6 byte6_1 (
    ._3A_INPUT({or_11_out[2], or_2_out[1], INPUT_1}), .in_2(INPUT[7]), .in_3(INPUT[6]), .in_4(INPUT[5]),
    .in_5(INPUT[4]), .in_6(INPUT[3]), .in_7(INPUT[2]), .in_8(INPUT[1]), .in_9(INPUT[0]),
    .OUTPUT(byte6_1_output));
  byte5 byte5_1 (
    ._3A_INPUT({or_12_out[2], or_2_out[1], INPUT_1}), .in_2(INPUT[7]), .in_3(INPUT[6]), .in_4(INPUT[5]),
    .in_5(INPUT[4]), .in_6(INPUT[3]), .in_7(INPUT[2]), .in_8(INPUT[1]), .in_9(INPUT[0]),
    .OUTPUT(byte5_1_output));
  byte3 byte3_1 (
    ._3A_INPUT({or_14_out[2], or_2_out[1], INPUT_1}), .in_2(INPUT[7]), .in_3(INPUT[6]), .in_4(INPUT[5]),
    .in_5(INPUT[4]), .in_6(INPUT[3]), .in_7(INPUT[2]), .in_8(INPUT[1]), .in_9(INPUT[0]),
    .OUTPUT(byte3_1_output));
  byte2 byte2_1 (
    ._3A_INPUT({or_15_out[2], or_2_out[1], INPUT_1}), .in_2(INPUT[7]), .in_3(INPUT[6]), .in_4(INPUT[5]),
    .in_5(INPUT[4]), .in_6(INPUT[3]), .in_7(INPUT[2]), .in_8(INPUT[1]), .in_9(INPUT[0]),
    .OUTPUT(byte2_1_output));
  byte1 byte1_1 (
    ._3A_INPUT({or_16_out[2], or_2_out[1], INPUT_1}), .in_2(INPUT[7]), .in_3(INPUT[6]), .in_4(INPUT[5]),
    .in_5(INPUT[4]), .in_6(INPUT[3]), .in_7(INPUT[2]), .in_8(INPUT[1]), .in_9(INPUT[0]),
    .OUTPUT(byte1_1_output));
  byte_0 byte_0_1 (
    ._3A_INPUT({or_17_out[2], or_2_out[1], INPUT_1}), .in_2(INPUT[7]), .in_3(INPUT[6]), .in_4(INPUT[5]),
    .in_5(INPUT[4]), .in_6(INPUT[3]), .in_7(INPUT[2]), .in_8(INPUT[1]), .in_9(INPUT[0]),
    .OUTPUT(byte_0_1_output));
  byte9 byte9_1 (
    ._3A_INPUT({or_8_out[2], or_2_out[1], INPUT_1}), .in_2(INPUT[7]), .in_3(INPUT[6]), .in_4(INPUT[5]),
    .in_5(INPUT[4]), .in_6(INPUT[3]), .in_7(INPUT[2]), .in_8(INPUT[1]), .in_9(INPUT[0]),
    .OUTPUT(byte9_1_output));
  byte4 byte4_1 (
    ._3A_INPUT({or_13_out[2], or_2_out[1], INPUT_1}), .in_2(INPUT[7]), .in_3(INPUT[6]), .in_4(INPUT[5]),
    .in_5(INPUT[4]), .in_6(INPUT[3]), .in_7(INPUT[2]), .in_8(INPUT[1]), .in_9(INPUT[0]),
    .OUTPUT(byte4_1_output));
  Multiplexer #(.select(4), .width(8)) multiplexer_1 (
    .in0(byte_0_1_output), .in1(byte1_1_output), .in2(byte2_1_output), .in3(byte3_1_output),
    .in4(byte4_1_output), .in5(byte5_1_output), .in6(byte6_1_output), .in7(byte7_1_output),
    .in8(byte8_1_output), .in9(byte9_1_output), .in10(byte10_1_output), .in11(byte11_1_output),
    .in12(byte12_1_output), .in13(byte13_1_output), .in14(_14_output), .in15(_15_output), .out(OUTPUT),
    .sel(ADDR));  // open: en
endmodule

module DR (
  input  [1:0] AND_GATE,
  input  [7:0] INPUT_BYTE,
  output [7:0] OUTPUT
);

  wire and_1_out;

  and and_1 (and_1_out, AND_GATE[0], AND_GATE[1]);
  D_Flip_Flop d_ff_1 (.clk(and_1_out), .D(INPUT_BYTE[7]), .Q(OUTPUT[7]));  // open: Qn, preset, en, reset
  D_Flip_Flop d_ff_2 (.clk(and_1_out), .D(INPUT_BYTE[6]), .Q(OUTPUT[6]));  // open: Qn, preset, en, reset
  D_Flip_Flop d_ff_3 (.clk(and_1_out), .D(INPUT_BYTE[5]), .Q(OUTPUT[5]));  // open: Qn, preset, en, reset
  D_Flip_Flop d_ff_4 (.clk(and_1_out), .D(INPUT_BYTE[4]), .Q(OUTPUT[4]));  // open: Qn, preset, en, reset
  D_Flip_Flop d_ff_5 (.clk(and_1_out), .D(INPUT_BYTE[3]), .Q(OUTPUT[3]));  // open: Qn, preset, en, reset
  D_Flip_Flop d_ff_6 (.clk(and_1_out), .D(INPUT_BYTE[2]), .Q(OUTPUT[2]));  // open: Qn, preset, en, reset
  D_Flip_Flop d_ff_7 (.clk(and_1_out), .D(INPUT_BYTE[1]), .Q(OUTPUT[1]));  // open: Qn, preset, en, reset
  D_Flip_Flop d_ff_8 (.clk(and_1_out), .D(INPUT_BYTE[0]), .Q(OUTPUT[0]));  // open: Qn, preset, en, reset
endmodule

module AR (
  input  CLK,
  input  [3:0] ADDR_INPUT,
  output [3:0] OUTPUT
);

  D_Flip_Flop d_ff_1 (.clk(CLK), .D(ADDR_INPUT[3]), .Q(OUTPUT[3]));  // open: Qn, preset, en, reset
  D_Flip_Flop d_ff_2 (.clk(CLK), .D(ADDR_INPUT[2]), .Q(OUTPUT[2]));  // open: Qn, preset, en, reset
  D_Flip_Flop d_ff_3 (.clk(CLK), .D(ADDR_INPUT[1]), .Q(OUTPUT[1]));  // open: Qn, preset, en, reset
  D_Flip_Flop d_ff_4 (.clk(CLK), .D(ADDR_INPUT[0]), .Q(OUTPUT[0]));  // open: Qn, preset, en, reset
endmodule

module MBR (
  input  [1:0] AND_GATE,
  input  [7:0] INPUT_BYTE,
  output [7:0] OUTPUT
);

  wire and_1_out;

  and and_1 (and_1_out, AND_GATE[0], AND_GATE[1]);
  D_Flip_Flop d_ff_1 (.clk(and_1_out), .D(INPUT_BYTE[7]), .Q(OUTPUT[7]));  // open: Qn, preset, en, reset
  D_Flip_Flop d_ff_2 (.clk(and_1_out), .D(INPUT_BYTE[6]), .Q(OUTPUT[6]));  // open: Qn, preset, en, reset
  D_Flip_Flop d_ff_3 (.clk(and_1_out), .D(INPUT_BYTE[5]), .Q(OUTPUT[5]));  // open: Qn, preset, en, reset
  D_Flip_Flop d_ff_4 (.clk(and_1_out), .D(INPUT_BYTE[4]), .Q(OUTPUT[4]));  // open: Qn, preset, en, reset
  D_Flip_Flop d_ff_5 (.clk(and_1_out), .D(INPUT_BYTE[3]), .Q(OUTPUT[3]));  // open: Qn, preset, en, reset
  D_Flip_Flop d_ff_6 (.clk(and_1_out), .D(INPUT_BYTE[2]), .Q(OUTPUT[2]));  // open: Qn, preset, en, reset
  D_Flip_Flop d_ff_7 (.clk(and_1_out), .D(INPUT_BYTE[1]), .Q(OUTPUT[1]));  // open: Qn, preset, en, reset
  D_Flip_Flop d_ff_8 (.clk(and_1_out), .D(INPUT_BYTE[0]), .Q(OUTPUT[0]));  // open: Qn, preset, en, reset
endmodule

module \new  (
  input  in_1,
  input  in_2,
  input  in_3,
  input  in_4,
  input  in_5,
  input  [9:0] _8
);

  wire and_2_out, clock_1_out, d_ff_1_qn, d_ff_2_qn, d_ff_3_qn, display_2_h1, display_2_h2, display_2_h3,
       display_2_h4, display_2_h5, display_2_h6, display_2_h7, display_2_l1, display_2_l2, display_2_l3,
       display_2_l4, display_2_l5, display_2_l6, display_2_l7, new_cu_1_alu_op, new_cu_1_alu_zero,
       new_cu_1_display_mux_a, new_cu_1_gr0_mux_a, new_cu_1_gr0_mux_b, new_cu_1_gr1_mux_a,
       new_cu_1_gr1_mux_b, new_cu_1_mar_mux_a, new_cu_1_mar_mux_b, new_cu_1_mbr_mux_c, new_cu_1_pc_mux_a,
       new_cu_1_pc_mux_b, new_cu_1_r_w, new_cu_1_stop, not_1_out, xor_1_out;
  wire [0:0] new_cu_1_a_out, new_cu_1_alu_l, new_cu_1_alu_r, new_cu_1_display_mux_b, new_cu_1_gr1,
       new_cu_1_ir, new_cu_1_mar, new_cu_1_mbr, new_cu_1_pc;
  wire [1:0] new_cu_1_gr0;
  wire [2:0] new_cu_1_mbr_mux_b;
  wire [3:0] alu_1_flag_register, IR_output, IR_output_2, MAR_output, multiplexer_3_out, multiplexer_4_out,
       PC_ADDER_result, PC_output;
  wire [7:0] _2_s_COMPLEMENT_output, A_OUT_output, alu_1_aout, ALU_L_output, ALU_R_output, DISPLAY_output,
       GR0_output, GR1_output, MBR_output, multiplexer_1_out, multiplexer_5_out, multiplexer_6_out,
       multiplexer_7_out, multiplexer_8_out, n8_bit_buffer_1_output, RAM_output1;

  D_Flip_Flop d_ff_1 (.Qn(d_ff_1_qn));  // open: clk, D, Q, preset, en, reset
  Clock #(.highDuration(3), .lowDuration(3)) clock_1 (.out(clock_1_out));
  D_Flip_Flop d_ff_2 (.clk(new_cu_1_stop), .D(d_ff_1_qn), .Qn(d_ff_2_qn));  // open: Q, preset, en, reset
  New_Ram RAM (
    .in_1(in_1), .in_2(in_2), .CLK(new_cu_1_gr0[1]), .R_0__W_1(new_cu_1_r_w), .AR_INPUT(MAR_output),
    .INPUT1(multiplexer_1_out), .OUTPUT1(RAM_output1));
  not not_1 (not_1_out, new_cu_1_r_w);
  and and_1 (new_cu_1_gr0[1], clock_1_out, d_ff_2_qn);
  Multiplexer #(.width(8)) multiplexer_1 (
    .in0(RAM_output1), .out(multiplexer_1_out), .sel(in_3), .en(not_1_out));  // open: in1
  Multiplexer #(.width(8)) multiplexer_2 (
    .in0(MBR_output), .out(multiplexer_1_out), .sel(in_4), .en(new_cu_1_r_w));  // open: in1
  PC_ADDER PC_ADDER (.INPUT(PC_output), .RESULT(PC_ADDER_result));
  register_4_bit PC (._3A_INPUT({new_cu_1_gr0[1], new_cu_1_pc[0]}), .INPUT(multiplexer_3_out), .OUTPUT(PC_output));
  Multiplexer #(.width(4)) multiplexer_3 (
    .in0(IR_output), .in1(PC_ADDER_result), .out(multiplexer_3_out), .sel(xor_1_out), .en(new_cu_1_pc_mux_b));
  xor xor_1 (xor_1_out, new_cu_1_pc_mux_a, and_2_out);
  NEW_CU new_cu_1 (
    .CLK(new_cu_1_gr0[1]), ._4_bit_INPUT(IR_output_2), ._444(in_5), .MAR_MUX_A(new_cu_1_mar_mux_a),
    .MAR_MUX_B(new_cu_1_mar_mux_b), .MAR(new_cu_1_mar[0]), .MBR_MUX_A(new_cu_1_mbr_mux_b[1]),
    .MBR_MUX_B(new_cu_1_mbr_mux_b[0]), .MBR_MUX_C(new_cu_1_mbr_mux_c), .MBR(new_cu_1_mbr[0]),
    .PC_MUX_A(new_cu_1_pc_mux_a), .PC_MUX_B(new_cu_1_pc_mux_b), .PC(new_cu_1_pc[0]), .R_W(new_cu_1_r_w),
    .IR(new_cu_1_ir[0]), .GR0_MUX_A(new_cu_1_gr0_mux_a), .GR0_MUX_B(new_cu_1_gr0_mux_b),
    .GR0(new_cu_1_gr0[0]), .GR1_MUX_A(new_cu_1_gr1_mux_a), .GR1_MUX_B(new_cu_1_gr1_mux_b),
    .GR1(new_cu_1_gr1[0]), .ALU_L(new_cu_1_alu_l[0]), .ALU_R(new_cu_1_alu_r[0]), .A_OUT(new_cu_1_a_out[0]),
    .MUX_ALPHA(new_cu_1_mbr_mux_b[2]), .ALU_OP(new_cu_1_alu_op), .ALU_ZERO(new_cu_1_alu_zero),
    .DISPLAY_MUX_A(new_cu_1_display_mux_a), .DISPLAY_MUX_B(new_cu_1_display_mux_b[0]), .STOP(new_cu_1_stop));
  Multiplexer #(.width(4)) multiplexer_4 (
    .in0(IR_output), .in1(PC_output), .out(multiplexer_4_out), .sel(new_cu_1_mar_mux_a),
    .en(new_cu_1_mar_mux_b));
  Register_8_bit IR (
    ._3A_INPUT({new_cu_1_gr0[1], new_cu_1_ir[0]}), .INPUT(MBR_output), .OUTPUT({IR_output_2, IR_output}));
  register_4_bit MAR (._3A_INPUT({new_cu_1_gr0[1], new_cu_1_mar[0]}), .INPUT(multiplexer_4_out), .OUTPUT(MAR_output));
  Multiplexer #(.select(3), .width(8)) multiplexer_5 (
    .in0(multiplexer_1_out), .in2(GR0_output), .in3(GR1_output), .in4(n8_bit_buffer_1_output),
    .in5(_2_s_COMPLEMENT_output), .out(multiplexer_5_out), .sel(new_cu_1_mbr_mux_b), .en(new_cu_1_mbr_mux_c));  // open: in1, in6, in7
  Register_8_bit MBR (._3A_INPUT({new_cu_1_gr0[1], new_cu_1_mbr[0]}), .INPUT(multiplexer_5_out), .OUTPUT(MBR_output));
  Multiplexer #(.width(8)) multiplexer_6 (
    .in0(MBR_output), .in1(A_OUT_output), .out(multiplexer_6_out), .sel(new_cu_1_gr1_mux_a),
    .en(new_cu_1_gr1_mux_b));
  Multiplexer #(.width(8)) multiplexer_7 (
    .in0(MBR_output), .in1(A_OUT_output), .out(multiplexer_7_out), .sel(new_cu_1_gr0_mux_a),
    .en(new_cu_1_gr0_mux_b));
  Register_8_bit GR1 (._3A_INPUT({new_cu_1_gr0[1], new_cu_1_gr1[0]}), .INPUT(multiplexer_6_out), .OUTPUT(GR1_output));
  Register_8_bit GR0 (._3A_INPUT(new_cu_1_gr0), .INPUT(multiplexer_7_out), .OUTPUT(GR0_output));
  _8_bit_Buffer u_8_bit_buffer_1 (.CLK(new_cu_1_gr0[1]), .OUTPUT(n8_bit_buffer_1_output), .INPUT(_8));
  Register_8_bit ALU_R (._3A_INPUT({new_cu_1_gr0[1], new_cu_1_alu_r[0]}), .INPUT(GR1_output), .OUTPUT(ALU_R_output));
  Register_8_bit ALU_L (._3A_INPUT({new_cu_1_gr0[1], new_cu_1_alu_l[0]}), .INPUT(GR0_output), .OUTPUT(ALU_L_output));
  D_Flip_Flop d_ff_3 (.Qn(d_ff_3_qn));  // open: clk, D, Q, preset, en, reset
  ALU alu_1 (
    .b_r(ALU_R_output), .ar(ALU_L_output), .contol0(new_cu_1_alu_op), .control1(d_ff_3_qn),
    .flag_register(alu_1_flag_register), .aout(alu_1_aout));
  _2_s_complement _2_s_COMPLEMENT (.INPUT(MBR_output), .OUTPUT(_2_s_COMPLEMENT_output));
  Register_8_bit A_OUT (._3A_INPUT({new_cu_1_gr0[1], new_cu_1_a_out[0]}), .INPUT(alu_1_aout), .OUTPUT(A_OUT_output));
  and and_2 (and_2_out, alu_1_flag_register[2], new_cu_1_alu_zero);
  Multiplexer #(.width(8)) multiplexer_8 (
    .in0(GR0_output), .in1(GR1_output), .out(multiplexer_8_out), .sel(new_cu_1_display_mux_a),
    .en(new_cu_1_display_mux_b[0]));
  Register_8_bit DISPLAY (
    ._3A_INPUT({new_cu_1_gr0[1], new_cu_1_display_mux_b[0]}), .INPUT(multiplexer_8_out),
    .OUTPUT(DISPLAY_output));
  _7_Segment_Display u_7_segment_display_1 (
    .g(display_2_h1), .f(display_2_h2), .a(display_2_h3), .b(display_2_h4), .e(display_2_h5),
    .d(display_2_h6), .c(display_2_h7));  // open: dp
  Display display_2 (
    .in_1(DISPLAY_output), .l5(display_2_l5), .l6(display_2_l6), .l7(display_2_l7), .h5(display_2_h5),
    .h6(display_2_h6), .h7(display_2_h7), .l1(display_2_l1), .l2(display_2_l2), .l3(display_2_l3),
    .l4(display_2_l4), .h1(display_2_h1), .h2(display_2_h2), .h3(display_2_h3), .h4(display_2_h4));
  _7_Segment_Display u_7_segment_display_2 (
    .g(display_2_l1), .f(display_2_l2), .a(display_2_l3), .b(display_2_l4), .e(display_2_l5),
    .d(display_2_l6), .c(display_2_l7));  // open: dp

  // Notes on the sheet:
  //   R/W BIT(0 to read from ram/1 to write to ram)
  //   BUS(DR)
  //   BUS (AR)
  //   keypad
  //   4
  //   5
  //   6
  //   7
  //   9
  //   2
  //   1
  //   0
  //   3
endmodule

module New_Ram (
  input  in_1,
  input  in_2,
  input  CLK,
  input  R_0__W_1,
  input  [3:0] AR_INPUT,
  input  [7:0] INPUT1,
  output [7:0] OUTPUT1
);

  wire d_ff_1_q, not_1_out;
  wire [3:0] AR_output;
  wire [7:0] multiplexer_1_out, RAM_output;

  AR AR (.CLK(CLK), .OUTPUT(AR_output), .ADDR_INPUT(AR_INPUT));
  RAM RAM (
    .INPUT_2(R_0__W_1), .ADDR(AR_output), .OUTPUT(RAM_output), .INPUT(OUTPUT1), .INPUT_1(CLK), .in_3(in_2),
    .in_1(in_1));
  D_Flip_Flop d_ff_1 (.Q(d_ff_1_q));  // open: clk, D, Qn, preset, en, reset
  DR dr_1 (.AND_GATE({2{CLK}}), .OUTPUT(OUTPUT1), .INPUT_BYTE(multiplexer_1_out));
  Multiplexer #(.width(8)) multiplexer_1 (
    .in0(RAM_output), .in1(INPUT1), .out(multiplexer_1_out), .sel(R_0__W_1), .en(not_1_out));
  not not_1 (not_1_out, d_ff_1_q);

  // Notes on the sheet:
  //   write/read control
  //   0 for read 1 for write
  //   DR
endmodule

module Register_8_bit (
  input  [1:0] _3A_INPUT,
  input  [7:0] INPUT,
  output [7:0] OUTPUT
);

  wire and_1_out;

  and and_1 (and_1_out, _3A_INPUT[0], _3A_INPUT[1]);
  D_Flip_Flop d_ff_1 (.clk(and_1_out), .D(INPUT[7]), .Q(OUTPUT[7]));  // open: Qn, preset, en, reset
  D_Flip_Flop d_ff_2 (.clk(and_1_out), .D(INPUT[6]), .Q(OUTPUT[6]));  // open: Qn, preset, en, reset
  D_Flip_Flop d_ff_3 (.clk(and_1_out), .D(INPUT[5]), .Q(OUTPUT[5]));  // open: Qn, preset, en, reset
  D_Flip_Flop d_ff_4 (.clk(and_1_out), .D(INPUT[4]), .Q(OUTPUT[4]));  // open: Qn, preset, en, reset
  D_Flip_Flop d_ff_5 (.clk(and_1_out), .D(INPUT[3]), .Q(OUTPUT[3]));  // open: Qn, preset, en, reset
  D_Flip_Flop d_ff_6 (.clk(and_1_out), .D(INPUT[2]), .Q(OUTPUT[2]));  // open: Qn, preset, en, reset
  D_Flip_Flop d_ff_7 (.clk(and_1_out), .D(INPUT[1]), .Q(OUTPUT[1]));  // open: Qn, preset, en, reset
  D_Flip_Flop d_ff_8 (.clk(and_1_out), .D(INPUT[0]), .Q(OUTPUT[0]));  // open: Qn, preset, en, reset
endmodule

module register_4_bit (
  input  [1:0] _3A_INPUT,
  input  [3:0] INPUT,
  output [3:0] OUTPUT
);

  wire and_1_out;

  and and_1 (and_1_out, _3A_INPUT[0], _3A_INPUT[1]);
  D_Flip_Flop d_ff_1 (.clk(and_1_out), .D(INPUT[3]), .Q(OUTPUT[3]));  // open: Qn, preset, en, reset
  D_Flip_Flop d_ff_2 (.clk(and_1_out), .D(INPUT[2]), .Q(OUTPUT[2]));  // open: Qn, preset, en, reset
  D_Flip_Flop d_ff_3 (.clk(and_1_out), .D(INPUT[1]), .Q(OUTPUT[1]));  // open: Qn, preset, en, reset
  D_Flip_Flop d_ff_4 (.clk(and_1_out), .D(INPUT[0]), .Q(OUTPUT[0]));  // open: Qn, preset, en, reset
endmodule

module Timer (
  input  CLK,
  input  INSTR,
  output _1ST,
  output _2ND,
  output _3RD,
  output _4TH,
  output _5TH,
  output _6TH,
  output _7TH,
  output _8TH
);

  wire and_1_out, d_ff_1_q, d_ff_2_q, d_ff_3_q, d_ff_4_q, d_ff_5_q, d_ff_6_q, d_ff_7_q, d_ff_8_q;

  and and_1 (and_1_out, CLK, INSTR);
  and and_2 (_1ST, INSTR, d_ff_1_q);
  D_Flip_Flop d_ff_1 (.clk(and_1_out), .D(d_ff_8_q), .Q(d_ff_1_q));  // open: Qn, preset, en, reset
  and and_3 (_2ND, INSTR, d_ff_2_q);
  D_Flip_Flop d_ff_2 (.clk(and_1_out), .D(d_ff_1_q), .Q(d_ff_2_q));  // open: Qn, preset, en, reset
  and and_4 (_3RD, INSTR, d_ff_3_q);
  D_Flip_Flop d_ff_3 (.clk(and_1_out), .D(d_ff_2_q), .Q(d_ff_3_q));  // open: Qn, preset, en, reset
  and and_5 (_4TH, INSTR, d_ff_4_q);
  D_Flip_Flop d_ff_4 (.clk(and_1_out), .D(d_ff_3_q), .Q(d_ff_4_q));  // open: Qn, preset, en, reset
  and and_6 (_5TH, INSTR, d_ff_5_q);
  D_Flip_Flop d_ff_5 (.clk(and_1_out), .D(d_ff_4_q), .Q(d_ff_5_q));  // open: Qn, preset, en, reset
  and and_7 (_6TH, INSTR, d_ff_6_q);
  D_Flip_Flop d_ff_6 (.clk(and_1_out), .D(d_ff_5_q), .Q(d_ff_6_q));  // open: Qn, preset, en, reset
  and and_8 (_7TH, INSTR, d_ff_7_q);
  D_Flip_Flop d_ff_7 (.clk(and_1_out), .D(d_ff_6_q), .Q(d_ff_7_q));  // open: Qn, preset, en, reset
  and and_9 (_8TH, INSTR, d_ff_8_q);
  D_Flip_Flop d_ff_8 (.clk(and_1_out), .D(d_ff_7_q), .Q(d_ff_8_q));  // open: Qn, preset, en, reset
endmodule

module timer (
);

  wire clock_1_out, d_ff_1_qn, d_ff_2_q, d_ff_3_q, d_ff_3_qn, d_ff_4_q, d_ff_4_qn, d_ff_5_q, d_ff_5_qn,
       or_1_out;

  Clock #(.highDuration(3), .lowDuration(3)) clock_1 (.out(clock_1_out));
  D_Flip_Flop d_ff_1 (.clk(clock_1_out), .D(or_1_out), .Qn(d_ff_1_qn));  // open: Q, preset, en, reset
  D_Flip_Flop #(.trigger("falling")) d_ff_2 (
    .clk(clock_1_out), .D(d_ff_5_q), .Q(d_ff_2_q), .preset(d_ff_1_qn));  // open: Qn, en, reset
  D_Flip_Flop #(.trigger("falling")) d_ff_3 (
    .clk(clock_1_out), .D(d_ff_2_q), .Q(d_ff_3_q), .Qn(d_ff_3_qn));  // open: preset, en, reset
  or or_1 (or_1_out, d_ff_3_qn, d_ff_4_qn, d_ff_5_qn);
  D_Flip_Flop #(.trigger("falling")) d_ff_4 (
    .clk(clock_1_out), .D(d_ff_3_q), .Q(d_ff_4_q), .Qn(d_ff_4_qn));  // open: preset, en, reset
  D_Flip_Flop #(.trigger("falling")) d_ff_5 (
    .clk(clock_1_out), .D(d_ff_4_q), .Q(d_ff_5_q), .Qn(d_ff_5_qn));  // open: preset, en, reset
  T_Flip_Flop t_ff_1 ();  // open: clk, T, Q, Qn, preset, reset, en
endmodule

module NewTimer (
  input  Control_Bit,
  input  CLK,
  output _1ST,
  output _2ND,
  output _3RD,
  output _4TH,
  output _5TH,
  output _6TH,
  output _7TH,
  output _8TH,
  output _9TH,
  output _10TH,
  output _11TH,
  output _12TH
);

  wire d_ff_1_qn, d_ff_2_q, d_ff_3_q, d_ff_3_qn, d_ff_4_q, d_ff_4_qn, d_ff_5_q, d_ff_5_qn, d_ff_6_q,
       d_ff_6_qn, d_ff_7_q, d_ff_7_qn, d_ff_8_q, d_ff_8_qn, d_ff_9_q, d_ff_9_qn, d_ff_10_q, d_ff_10_qn,
       d_ff_11_q, d_ff_11_qn, d_ff_12_q, d_ff_12_qn, d_ff_13_q, d_ff_13_qn, or_1_out;

  D_Flip_Flop d_ff_1 (.clk(CLK), .D(or_1_out), .Qn(d_ff_1_qn));  // open: Q, preset, en, reset
  D_Flip_Flop #(.trigger("falling")) d_ff_2 (
    .clk(CLK), .D(d_ff_13_q), .Q(d_ff_2_q), .preset(d_ff_1_qn));  // open: Qn, en, reset
  and TICK_1 (_1ST, Control_Bit, d_ff_2_q);
  and TICK_2 (_2ND, Control_Bit, d_ff_3_q);
  D_Flip_Flop #(.trigger("falling")) d_ff_3 (
    .clk(CLK), .D(d_ff_2_q), .Q(d_ff_3_q), .Qn(d_ff_3_qn));  // open: preset, en, reset
  D_Flip_Flop #(.trigger("falling")) d_ff_4 (
    .clk(CLK), .D(d_ff_3_q), .Q(d_ff_4_q), .Qn(d_ff_4_qn));  // open: preset, en, reset
  or or_1 (or_1_out, d_ff_3_qn, d_ff_4_qn, d_ff_5_qn, d_ff_6_qn, d_ff_7_qn, d_ff_8_qn, d_ff_9_qn, d_ff_10_qn, d_ff_11_qn, d_ff_12_qn, d_ff_13_qn);
  and TICK_3 (_3RD, Control_Bit, d_ff_4_q);
  D_Flip_Flop #(.trigger("falling")) d_ff_5 (
    .clk(CLK), .D(d_ff_4_q), .Q(d_ff_5_q), .Qn(d_ff_5_qn));  // open: preset, en, reset
  and TICK_4 (_4TH, Control_Bit, d_ff_5_q);
  D_Flip_Flop #(.trigger("falling")) d_ff_6 (
    .clk(CLK), .D(d_ff_5_q), .Q(d_ff_6_q), .Qn(d_ff_6_qn));  // open: preset, en, reset
  and TICK_5 (_5TH, Control_Bit, d_ff_6_q);
  and TICK_6 (_6TH, Control_Bit, d_ff_7_q);
  D_Flip_Flop #(.trigger("falling")) d_ff_7 (
    .clk(CLK), .D(d_ff_6_q), .Q(d_ff_7_q), .Qn(d_ff_7_qn));  // open: preset, en, reset
  D_Flip_Flop #(.trigger("falling")) d_ff_8 (
    .clk(CLK), .D(d_ff_7_q), .Q(d_ff_8_q), .Qn(d_ff_8_qn));  // open: preset, en, reset
  and TICK_7 (_7TH, Control_Bit, d_ff_8_q);
  D_Flip_Flop #(.trigger("falling")) d_ff_9 (
    .clk(CLK), .D(d_ff_8_q), .Q(d_ff_9_q), .Qn(d_ff_9_qn));  // open: preset, en, reset
  and TICK_8 (_8TH, Control_Bit, d_ff_9_q);
  and TICK_9 (_9TH, Control_Bit, d_ff_10_q);
  D_Flip_Flop #(.trigger("falling")) d_ff_10 (
    .clk(CLK), .D(d_ff_9_q), .Q(d_ff_10_q), .Qn(d_ff_10_qn));  // open: preset, en, reset
  D_Flip_Flop #(.trigger("falling")) d_ff_11 (
    .clk(CLK), .D(d_ff_10_q), .Q(d_ff_11_q), .Qn(d_ff_11_qn));  // open: preset, en, reset
  and TICK_10 (_10TH, Control_Bit, d_ff_11_q);
  D_Flip_Flop #(.trigger("falling")) d_ff_12 (
    .clk(CLK), .D(d_ff_11_q), .Q(d_ff_12_q), .Qn(d_ff_12_qn));  // open: preset, en, reset
  and TICK_11 (_11TH, Control_Bit, d_ff_12_q);
  and TICK_12 (_12TH, Control_Bit, d_ff_13_q);
  D_Flip_Flop #(.trigger("falling")) d_ff_13 (
    .clk(CLK), .D(d_ff_12_q), .Q(d_ff_13_q), .Qn(d_ff_13_qn));  // open: preset, en, reset
endmodule

module NEW_CU (
  input  CLK,
  input  [3:0] _4_bit_INPUT,
  input  _444,
  output MAR_MUX_A,
  output MAR_MUX_B,
  output MAR,
  output MBR_MUX_A,
  output MBR_MUX_B,
  output MBR_MUX_C,
  output MBR,
  output PC_MUX_A,
  output PC_MUX_B,
  output PC,
  output R_W,
  output IR,
  output GR0_MUX_A,
  output GR0_MUX_B,
  output GR0,
  output GR1_MUX_A,
  output GR1_MUX_B,
  output GR1,
  output ALU_L,
  output ALU_R,
  output A_OUT,
  output MUX_ALPHA,
  output ALU_OP,
  output ALU_ZERO,
  output DISPLAY_MUX_A,
  output DISPLAY_MUX_B,
  output STOP
);

  wire _1__1st, _1__4th, _1__5th, _1__7th, _1__8th, _1__9th, _1__11th, _2__1st, _2__4th, _2__5th, _2__7th,
       _2__8th, _2__9th, _2__11th, _3__1st, _3__4th, _3__5th, _3__7th, _3__10th, _3__11th, _3__12th, _4__1st,
       _4__4th, _4__5th, _4__7th, _4__10th, _4__11th, _4__12th, _5__1st, _5__4th, _5__5th, _5__7th, _5__10th,
       _5__11th, _5__12th, _6__1st, _6__4th, _6__5th, _6__7th, _6__10th, _6__11th, _6__12th, _7__1st,
       _7__4th, _7__5th, _7__7th, _7__9th, _8__1st, _8__4th, _8__5th, _8__11th, _9__1st, _9__4th, _9__5th,
       _9__8th, _9__11th, _10__1st, _10__4th, _10__5th, _10__8th, _10__11th, _11__1st, _11__4th, _11__5th,
       _11__7th, _11__8th, _11__11th, _12__1st, _12__4th, _12__5th, _12__7th, _12__8th, _12__11th, _13__1st,
       _13__4th, _13__5th, _13__7th, _13__8th, _13__10th, _13__11th, _14__1st, _14__4th, _14__5th, _15__1st,
       _15__4th, _15__5th, _15__7th, _15__8th, _15__9th, _15__11th, _16__1st, _16__4th, _16__5th, _16__7th,
       _16__8th, _16__9th, _16__11th, decoder_1_out0, decoder_1_out1, decoder_1_out2, decoder_1_out3,
       decoder_1_out4, decoder_1_out5, decoder_1_out6, decoder_1_out7, decoder_1_out8, decoder_1_out9,
       decoder_1_out10, decoder_1_out11, decoder_1_out12, decoder_1_out13, decoder_1_out14, decoder_1_out15,
       or_1_out, or_2_out, or_3_out, or_4_out, or_5_out, or_6_out, or_7_out, or_8_out, or_9_out, or_10_out,
       or_11_out, or_12_out;

  Decoder #(.select(4)) decoder_1 (
    .out0(decoder_1_out0), .out1(decoder_1_out1), .out2(decoder_1_out2), .out3(decoder_1_out3),
    .out4(decoder_1_out4), .out5(decoder_1_out5), .out6(decoder_1_out6), .out7(decoder_1_out7),
    .out8(decoder_1_out8), .out9(decoder_1_out9), .out10(decoder_1_out10), .out11(decoder_1_out11),
    .out12(decoder_1_out12), .out13(decoder_1_out13), .out14(decoder_1_out14), .out15(decoder_1_out15),
    .sel(_4_bit_INPUT));  // open: en
  NewTimer _1 (
    .Control_Bit(decoder_1_out0), .CLK(CLK), ._1ST(_1__1st), ._4TH(_1__4th), ._5TH(_1__5th), ._7TH(_1__7th),
    ._8TH(_1__8th), ._9TH(_1__9th), ._11TH(_1__11th));  // open: _2ND, _3RD, _6TH, _10TH, _12TH
  NewTimer _2 (
    .Control_Bit(decoder_1_out1), .CLK(CLK), ._1ST(_2__1st), ._4TH(_2__4th), ._5TH(_2__5th), ._7TH(_2__7th),
    ._8TH(_2__8th), ._9TH(_2__9th), ._11TH(_2__11th));  // open: _2ND, _3RD, _6TH, _10TH, _12TH
  NewTimer _3 (
    .Control_Bit(decoder_1_out2), .CLK(CLK), ._1ST(_3__1st), ._4TH(_3__4th), ._5TH(_3__5th), ._7TH(_3__7th),
    ._10TH(_3__10th), ._11TH(_3__11th), ._12TH(_3__12th));  // open: _2ND, _3RD, _6TH, _8TH, _9TH
  NewTimer _4 (
    .Control_Bit(decoder_1_out3), .CLK(CLK), ._1ST(_4__1st), ._4TH(_4__4th), ._5TH(_4__5th), ._7TH(_4__7th),
    ._10TH(_4__10th), ._11TH(_4__11th), ._12TH(_4__12th));  // open: _2ND, _3RD, _6TH, _8TH, _9TH
  NewTimer _5 (
    .Control_Bit(decoder_1_out4), .CLK(CLK), ._1ST(_5__1st), ._4TH(_5__4th), ._5TH(_5__5th), ._7TH(_5__7th),
    ._10TH(_5__10th), ._11TH(_5__11th), ._12TH(_5__12th));  // open: _2ND, _3RD, _6TH, _8TH, _9TH
  NewTimer _6 (
    .Control_Bit(decoder_1_out5), .CLK(CLK), ._1ST(_6__1st), ._4TH(_6__4th), ._5TH(_6__5th), ._7TH(_6__7th),
    ._10TH(_6__10th), ._11TH(_6__11th), ._12TH(_6__12th));  // open: _2ND, _3RD, _6TH, _8TH, _9TH
  NewTimer _7 (
    .Control_Bit(decoder_1_out6), .CLK(CLK), ._1ST(_7__1st), ._4TH(_7__4th), ._5TH(_7__5th), ._7TH(_7__7th),
    ._9TH(_7__9th));  // open: _2ND, _3RD, _6TH, _8TH, _10TH, _11TH, _12TH
  NewTimer _8 (
    .Control_Bit(decoder_1_out7), .CLK(CLK), ._1ST(_8__1st), ._4TH(_8__4th), ._5TH(_8__5th), ._11TH(_8__11th));  // open: _2ND, _3RD, _6TH, _7TH, _8TH, _9TH, _10TH, _12TH
  NewTimer _9 (
    .Control_Bit(decoder_1_out8), .CLK(CLK), ._1ST(_9__1st), ._4TH(_9__4th), ._5TH(_9__5th), ._8TH(_9__8th),
    ._11TH(_9__11th));  // open: _2ND, _3RD, _6TH, _7TH, _9TH, _10TH, _12TH
  NewTimer _10 (
    .Control_Bit(decoder_1_out9), .CLK(CLK), ._1ST(_10__1st), ._4TH(_10__4th), ._5TH(_10__5th),
    ._8TH(_10__8th), ._11TH(_10__11th));  // open: _2ND, _3RD, _6TH, _7TH, _9TH, _10TH, _12TH
  NewTimer _11 (
    .Control_Bit(decoder_1_out10), .CLK(CLK), ._1ST(_11__1st), ._4TH(_11__4th), ._5TH(_11__5th),
    ._7TH(_11__7th), ._8TH(_11__8th), ._11TH(_11__11th));  // open: _2ND, _3RD, _6TH, _9TH, _10TH, _12TH
  NewTimer _12 (
    .Control_Bit(decoder_1_out11), .CLK(CLK), ._1ST(_12__1st), ._4TH(_12__4th), ._5TH(_12__5th),
    ._7TH(_12__7th), ._8TH(_12__8th), ._11TH(_12__11th));  // open: _2ND, _3RD, _6TH, _9TH, _10TH, _12TH
  NewTimer _13 (
    .Control_Bit(decoder_1_out12), .CLK(CLK), ._1ST(_13__1st), ._4TH(_13__4th), ._5TH(_13__5th),
    ._7TH(_13__7th), ._8TH(_13__8th), ._10TH(_13__10th), ._11TH(_13__11th));  // open: _2ND, _3RD, _6TH, _9TH, _12TH
  NewTimer _14 (
    .Control_Bit(decoder_1_out13), .CLK(CLK), ._1ST(_14__1st), ._4TH(_14__4th), ._5TH(_14__5th));  // open: _2ND, _3RD, _6TH, _7TH, _8TH, _9TH, _10TH, _11TH, _12TH
  NewTimer _15 (
    .Control_Bit(decoder_1_out14), .CLK(CLK), ._1ST(_15__1st), ._4TH(_15__4th), ._5TH(_15__5th),
    ._7TH(_15__7th), ._8TH(_15__8th), ._9TH(_15__9th), ._11TH(_15__11th));  // open: _2ND, _3RD, _6TH, _10TH, _12TH
  NewTimer _16 (
    .Control_Bit(decoder_1_out15), .CLK(CLK), ._1ST(_16__1st), ._4TH(_16__4th), ._5TH(_16__5th),
    ._7TH(_16__7th), ._8TH(_16__8th), ._9TH(_16__9th), ._11TH(_16__11th));  // open: _2ND, _3RD, _6TH, _10TH, _12TH
  or or_1 (or_1_out, _3__10th, _3__11th);
  or or_2 (or_2_out, _4__10th, _4__11th);
  or or_3 (or_3_out, _1__1st, _7__1st, _8__1st, _9__1st, _10__1st, _11__1st, _12__1st, _13__1st);
  or or_4 (or_4_out, or_3_out, _14__1st, _15__1st, _16__1st);
  or or_5 (or_5_out, _15__8th, _16__8th);
  or or_6 (or_6_out, _11__11th, _12__11th, _15__11th, _16__11th);
  or or_7 (or_7_out, _2__4th, _7__4th, _8__4th, _9__4th, _10__4th, _11__4th);
  or or_8 (or_8_out, _9__11th, _10__11th);
  or or_9 (or_9_out, or_7_out, _12__4th, _13__4th, _14__4th, _15__4th, _16__4th);
  or or_10 (or_10_out, _11__7th, _12__7th);
  or or_11 (or_11_out, _3__5th, _7__5th, _8__5th, _9__5th, _10__5th, _11__5th);
  or or_12 (or_12_out, or_11_out, _12__5th, _13__5th, _14__5th, _15__5th, _16__5th);
  or u_MAR_MUX_A (MAR_MUX_A, or_4_out, _2__1st, _3__1st, _4__1st, _5__1st, _6__1st);
  or u_MAR (MAR, or_4_out, _2__1st, _3__1st, _3__7th, _4__1st, _4__7th, _5__1st, _5__7th, _6__1st, _6__7th);
  or u_MAR_MUX_B (MAR_MUX_B, or_4_out, _2__1st, _3__1st, _3__7th, _4__1st, _4__7th, _5__1st, _5__7th, _6__1st, _6__7th);
  or u_MBR_MUX_A (MBR_MUX_A, _3__7th, _4__7th, _16__7th, _15__7th);
  or u_MBR_MUX_B (MBR_MUX_B, _4__7th, or_5_out, _16__7th);
  or u_MBR_MUX_c (MBR_MUX_C, _1__4th, or_9_out, _3__4th, _3__7th, _4__4th, _4__7th, _5__4th, _5__10th, _6__4th, _6__10th, or_10_out, _15__7th, or_5_out, _16__7th);
  or u_MBR (MBR, _1__4th, or_9_out, _3__4th, _3__7th, _4__4th, _4__7th, _5__4th, _5__10th, _6__4th, _6__10th, _16__7th, or_10_out, _15__7th, or_5_out);
  or u_PC_MUX_A (PC_MUX_A, _1__11th, _2__11th, _3__12th, _4__12th, _5__12th, _6__12th, _7__9th, _13__11th, or_6_out, or_8_out);
  or PC_MUX__B (PC_MUX_B, _1__11th, _2__11th, _3__12th, _4__12th, _5__12th, _6__12th, _7__9th, or_6_out, _13__11th, or_8_out);
  or u_PC (PC, _1__11th, _2__11th, _3__12th, _4__12th, _5__12th, _6__12th, _7__9th, _13__11th, or_6_out, or_8_out);
  or I_O (R_W, or_1_out, or_2_out);
  or u_IR (IR, _1__5th, _2__5th, or_12_out, _4__5th, _5__5th, _6__5th);
  or u_GR0_MUX_A (GR0_MUX_A, _1__9th, _13__10th);
  or u_GR0_MUX_B (GR0_MUX_B, _1__9th, _5__11th, _13__10th, _11__8th, _15__9th);
  or u_GR0 (GR0, _1__9th, _5__11th, _13__10th, _11__8th, _15__9th);
  buf u_GR1_MUX_A (GR1_MUX_A, _2__9th);  // OR_Gate
  or u_GR1_MUX_B (GR1_MUX_B, _2__9th, _6__11th, _12__8th, _16__9th);
  or u_GR1 (GR1, _2__9th, _6__11th, _12__8th, _16__9th);
  or ALU__L (ALU_L, _1__7th, _2__7th, _7__7th, _13__7th);
  or u_ALU_R (ALU_R, _1__7th, _2__7th, _7__7th, _13__7th);
  or u_A_OUT (A_OUT, _1__8th, _2__8th, _13__8th);
  or or_13 (MUX_ALPHA, or_10_out, or_5_out, _444);
  or or_14 (ALU_OP, _7__9th, _13__8th, _444);
  or or_15 (ALU_ZERO, _7__9th, _444);
  buf or_16 (DISPLAY_MUX_A, _10__8th);  // OR_Gate
  or or_17 (DISPLAY_MUX_B, _9__8th, _10__8th);
  buf or_18 (STOP, _8__11th);  // OR_Gate

  // Notes on the sheet:
  //   Wait for all signals before shutting down
endmodule

module PC_ADDER (
  input  [3:0] INPUT,
  output [3:0] RESULT
);

  wire [3:0] d_ff_4_qn;

  D_Flip_Flop d_ff_1 (.Q(d_ff_4_qn[3]));  // open: clk, D, Qn, preset, en, reset
  D_Flip_Flop d_ff_2 (.Q(d_ff_4_qn[2]));  // open: clk, D, Qn, preset, en, reset
  D_Flip_Flop d_ff_3 (.Q(d_ff_4_qn[1]));  // open: clk, D, Qn, preset, en, reset
  D_Flip_Flop d_ff_4 (.Qn(d_ff_4_qn[0]));  // open: clk, D, Q, preset, en, reset
  Adder #(.width(4)) adder_1 (.a(d_ff_4_qn), .b(INPUT), .out(RESULT));  // open: cin, cout
endmodule

module ALU (
  input  control1,
  input  contol0,
  input  [7:0] b_r,
  input  [7:0] ar,
  output [3:0] flag_register,
  output [7:0] aout
);

  wire adder_1_out, adder_2_cout, adder_2_out, adder_3_cout, adder_3_out, adder_4_cout, adder_4_out,
       adder_5_cout, adder_5_out, adder_6_cout, adder_6_out, adder_7_cout, adder_7_out, adder_8_cout,
       adder_8_out, and_1_out, and_2_out, and_3_out, and_4_out, and_5_out, and_6_out, and_7_out, and_8_out,
       and_9_out, and_10_out, and_11_out, and_12_out, and_13_out, and_14_out, and_15_out, and_16_out,
       and_17_out, and_18_out, and_19_out, and_20_out, and_21_out, and_22_out, and_23_out, and_24_out,
       and_25_out, and_26_out, and_27_out, and_28_out, and_29_out, and_30_out, and_31_out, and_32_out,
       and_33_out, and_34_out, and_35_out, and_36_out, and_37_out, and_38_out, and_39_out, and_40_out,
       and_41_out, and_operation_out, not_1_out, not_2_out, not_3_out, not_4_out, not_5_out, or_2_out,
       or_3_out, or_4_out, or_5_out, or_6_out, or_7_out, or_8_out, or_9_out, or_10_out, or_11_out, or_12_out,
       or_13_out, or_14_out, or_15_out, or_16_out, or_operation_out, select_between_or_and_and_out,
       xor_1_out, xor_2_out, xor_3_out, xor_4_out, xor_5_out, xor_6_out, xor_7_out, xor_8_out;

  and and_1 (and_1_out, not_2_out, not_1_out, adder_1_out);
  not not_1 (not_1_out, ar[7]);
  not not_2 (not_2_out, xor_1_out);
  xor xor_1 (xor_1_out, b_r[7], contol0);
  and and_2 (and_2_out, ar[7], xor_1_out, not_3_out);
  not not_3 (not_3_out, adder_1_out);
  Adder #(.width(1)) adder_1 (.a(xor_1_out), .b(ar[7]), .out(adder_1_out), .cin(adder_2_cout), .cout(flag_register[1]));
  xor xor_2 (xor_2_out, b_r[6], contol0);
  Adder #(.width(1)) adder_2 (.a(xor_2_out), .b(ar[6]), .out(adder_2_out), .cin(adder_3_cout), .cout(adder_2_cout));
  xor xor_3 (xor_3_out, b_r[5], contol0);
  Adder #(.width(1)) adder_3 (.a(xor_3_out), .b(ar[5]), .out(adder_3_out), .cin(adder_4_cout), .cout(adder_3_cout));
  xor xor_4 (xor_4_out, b_r[4], contol0);
  Adder #(.width(1)) adder_4 (.a(xor_4_out), .b(ar[4]), .out(adder_4_out), .cin(adder_5_cout), .cout(adder_4_cout));
  xor xor_5 (xor_5_out, b_r[3], contol0);
  Adder #(.width(1)) adder_5 (.a(xor_5_out), .b(ar[3]), .out(adder_5_out), .cin(adder_6_cout), .cout(adder_5_cout));
  xor xor_6 (xor_6_out, b_r[2], contol0);
  Adder #(.width(1)) adder_6 (.a(xor_6_out), .b(ar[2]), .out(adder_6_out), .cin(adder_7_cout), .cout(adder_6_cout));
  xor xor_7 (xor_7_out, b_r[1], contol0);
  Adder #(.width(1)) adder_7 (.a(xor_7_out), .b(ar[1]), .out(adder_7_out), .cin(adder_8_cout), .cout(adder_7_cout));
  xor xor_8 (xor_8_out, b_r[0], contol0);
  Adder #(.width(1)) adder_8 (.a(xor_8_out), .b(ar[0]), .out(adder_8_out), .cin(contol0), .cout(adder_8_cout));
  or or_1 (flag_register[0], and_1_out, and_2_out);
  not not_4 (not_4_out, contol0);
  or or_operation (or_operation_out, b_r[7], ar[7]);
  and and_operation (and_operation_out, b_r[7], ar[7]);
  or or_2 (or_2_out, b_r[6], ar[6]);
  and and_3 (and_3_out, b_r[6], ar[6]);
  or or_3 (or_3_out, b_r[5], ar[5]);
  and and_4 (and_4_out, b_r[5], ar[5]);
  or or_4 (or_4_out, b_r[4], ar[4]);
  and and_5 (and_5_out, b_r[4], ar[4]);
  or or_5 (or_5_out, b_r[3], ar[3]);
  and and_6 (and_6_out, b_r[3], ar[3]);
  or or_6 (or_6_out, b_r[2], ar[2]);
  and and_7 (and_7_out, b_r[2], ar[2]);
  or or_7 (or_7_out, b_r[1], ar[1]);
  and and_8 (and_8_out, b_r[1], ar[1]);
  or or_8 (or_8_out, b_r[0], ar[0]);
  and and_9 (and_9_out, b_r[0], ar[0]);
  and and_10 (and_10_out, not_4_out, or_operation_out);
  and and_11 (and_11_out, not_4_out, or_2_out);
  and and_12 (and_12_out, not_4_out, or_3_out);
  and and_13 (and_13_out, not_4_out, or_4_out);
  and and_14 (and_14_out, not_4_out, or_5_out);
  and and_15 (and_15_out, not_4_out, or_6_out);
  and and_16 (and_16_out, not_4_out, or_7_out);
  and and_17 (and_17_out, not_4_out, or_8_out);
  or select_between_or_and_and (select_between_or_and_and_out, and_10_out, and_18_out);
  and and_18 (and_18_out, and_operation_out, contol0);
  or or_9 (or_9_out, and_11_out, and_19_out);
  and and_19 (and_19_out, contol0, and_3_out);
  or or_10 (or_10_out, and_12_out, and_20_out);
  and and_20 (and_20_out, contol0, and_4_out);
  or or_11 (or_11_out, and_13_out, and_21_out);
  and and_21 (and_21_out, contol0, and_5_out);
  or or_12 (or_12_out, and_14_out, and_22_out);
  and and_22 (and_22_out, contol0, and_6_out);
  or or_13 (or_13_out, and_15_out, and_23_out);
  and and_23 (and_23_out, contol0, and_7_out);
  or or_14 (or_14_out, and_16_out, and_24_out);
  and and_24 (and_24_out, contol0, and_8_out);
  or or_15 (or_15_out, and_17_out, and_25_out);
  and and_25 (and_25_out, contol0, and_9_out);
  not not_5 (not_5_out, control1);
  and and_26 (and_26_out, not_5_out, select_between_or_and_and_out);
  and and_27 (and_27_out, not_5_out, or_9_out);
  and and_28 (and_28_out, not_5_out, or_10_out);
  and and_29 (and_29_out, not_5_out, or_11_out);
  and and_30 (and_30_out, not_5_out, or_12_out);
  and and_31 (and_31_out, not_5_out, or_13_out);
  and and_32 (and_32_out, not_5_out, or_14_out);
  and and_33 (and_33_out, not_5_out, or_15_out);
  and and_34 (and_34_out, control1, adder_1_out);
  and and_35 (and_35_out, control1, adder_2_out);
  and and_36 (and_36_out, control1, adder_3_out);
  and and_37 (and_37_out, control1, adder_4_out);
  and and_38 (and_38_out, control1, adder_5_out);
  and and_39 (and_39_out, control1, adder_6_out);
  and and_40 (and_40_out, control1, adder_7_out);
  and and_41 (and_41_out, control1, adder_8_out);
  not not_6 (flag_register[2], or_16_out);
  or or_16 (or_16_out, aout[0], aout[1], aout[2], aout[3], aout[4], aout[5], aout[6], aout[7]);
  or or_17 (aout[7], and_34_out, and_26_out);
  or or_18 (aout[6], and_35_out, and_27_out);
  or or_19 (aout[5], and_36_out, and_28_out);
  or or_20 (aout[4], and_37_out, and_29_out);
  or or_21 (aout[3], and_38_out, and_30_out);
  or or_22 (aout[2], and_39_out, and_31_out);
  or or_23 (aout[1], and_40_out, and_32_out);
  or or_24 (aout[0], and_41_out, and_33_out);

  assign flag_register[3] = aout[7];

  // Notes on the sheet:
  //   c0=0,c1=0  A AND B
  //   co=1,c1=0   A OR B
  //   c0=0,c1=1 A +B
  //   c0=1, c1=1 A-B
  //   overflow check
  //   add one or zero depending on the operation
  //   overflow check
  //   select between adder and logic
  //   0 overf, 1car,2zero,3neg
endmodule

module _8_bit_Buffer (
  input  CLK,
  input  [9:0] INPUT,
  output [7:0] OUTPUT
);

  wire undriven, undriven_2, undriven_3, undriven_4;
  wire [3:0] priority_encoder_1_p1;

  D_Flip_Flop d_ff_1 (.clk(CLK), .D(undriven), .Q(OUTPUT[7]));  // open: Qn, preset, en, reset
  D_Flip_Flop d_ff_2 (.clk(CLK), .D(undriven_2), .Q(OUTPUT[6]));  // open: Qn, preset, en, reset
  D_Flip_Flop d_ff_3 (.clk(CLK), .D(undriven_3), .Q(OUTPUT[5]));  // open: Qn, preset, en, reset
  D_Flip_Flop d_ff_4 (.clk(CLK), .D(undriven_4), .Q(OUTPUT[4]));  // open: Qn, preset, en, reset
  D_Flip_Flop d_ff_5 (.clk(CLK), .D(priority_encoder_1_p1[3]), .Q(OUTPUT[3]));  // open: Qn, preset, en, reset
  D_Flip_Flop d_ff_6 (.clk(CLK), .D(priority_encoder_1_p1[2]), .Q(OUTPUT[2]));  // open: Qn, preset, en, reset
  D_Flip_Flop d_ff_7 (.clk(CLK), .D(priority_encoder_1_p1[1]), .Q(OUTPUT[1]));  // open: Qn, preset, en, reset
  D_Flip_Flop d_ff_8 (.clk(CLK), .D(priority_encoder_1_p1[0]), .Q(OUTPUT[0]));  // open: Qn, preset, en, reset
  // Priority_Encoder #(.select(4)) priority_encoder_1: pin names not known; wires that end beside it: priority_encoder_1_p1
endmodule

module Display (
  input  [7:0] in_1,
  output l1,
  output l2,
  output l3,
  output l4,
  output h1,
  output h2,
  output h3,
  output h4,
  output l5,
  output l6,
  output l7,
  output h5,
  output h6,
  output h7
);

  wire and_1_out, and_2_out, and_3_out, and_4_out, and_5_out, and_6_out, and_7_out, and_8_out, and_9_out,
       and_10_out, and_11_out, and_12_out, and_13_out, and_14_out, and_15_out, and_16_out, and_17_out,
       and_18_out, and_19_out, and_20_out, and_21_out, and_22_out, and_23_out, and_24_out, and_25_out,
       and_26_out, and_27_out, and_28_out, and_29_out, and_30_out, and_31_out, and_32_out, not_1_out,
       not_2_out, not_3_out, not_4_out, not_5_out, not_6_out, not_7_out, not_8_out, not_9_out, not_10_out,
       not_11_out, not_12_out, not_13_out, not_14_out, not_15_out, not_16_out, not_17_out, not_18_out,
       not_19_out, not_20_out, not_21_out, not_22_out, not_23_out, not_24_out, not_25_out, not_26_out,
       not_27_out, not_28_out, not_29_out, not_30_out, not_31_out, not_32_out, not_33_out, not_34_out,
       not_35_out, not_36_out, not_37_out, not_38_out, not_39_out, not_40_out, not_41_out, not_42_out,
       not_43_out, not_44_out, not_45_out, not_46_out, not_47_out, not_48_out, not_49_out, not_50_out,
       not_51_out, not_52_out, not_53_out, not_54_out, not_55_out, not_56_out, not_57_out, not_58_out,
       not_59_out, not_60_out, not_61_out, not_62_out, not_63_out, not_64_out;

  not not_1 (not_1_out, in_1[3]);
  not not_2 (not_2_out, in_1[2]);
  not not_3 (not_3_out, in_1[1]);
  not not_4 (not_4_out, in_1[0]);
  and and_1 (and_1_out, not_4_out, not_3_out, not_2_out, not_1_out);
  or or_1 (l5, and_1_out, and_2_out, and_7_out, and_9_out, and_10_out, and_12_out, and_13_out, and_14_out, and_16_out, and_15_out);
  not not_5 (not_5_out, in_1[3]);
  not not_6 (not_6_out, in_1[3]);
  not not_7 (not_7_out, in_1[2]);
  not not_8 (not_8_out, in_1[2]);
  not not_9 (not_9_out, in_1[1]);
  not not_10 (not_10_out, in_1[0]);
  and and_2 (and_2_out, not_10_out, in_1[1], not_7_out, not_6_out);
  and and_3 (and_3_out, in_1[0], not_9_out, not_8_out, not_5_out);
  not not_11 (not_11_out, in_1[3]);
  not not_12 (not_12_out, in_1[2]);
  not not_13 (not_13_out, in_1[1]);
  not not_14 (not_14_out, in_1[0]);
  and and_4 (and_4_out, in_1[0], in_1[1], not_12_out, not_11_out);
  and and_5 (and_5_out, not_14_out, not_13_out, in_1[2], not_16_out);
  not not_15 (not_15_out, in_1[3]);
  not not_16 (not_16_out, in_1[3]);
  not not_17 (not_17_out, in_1[1]);
  and and_6 (and_6_out, in_1[0], not_17_out, in_1[2], not_15_out);
  or or_2 (l6, and_1_out, and_2_out, and_4_out, and_6_out, and_7_out, and_9_out, and_12_out, and_13_out, and_14_out, and_16_out);
  not not_18 (not_18_out, in_1[3]);
  not not_19 (not_19_out, in_1[0]);
  and and_7 (and_7_out, not_19_out, in_1[1], in_1[2], not_18_out);
  and and_8 (and_8_out, in_1[0], in_1[1], in_1[2], not_20_out);
  not not_20 (not_20_out, in_1[3]);
  or or_3 (l7, and_1_out, and_3_out, and_4_out, and_5_out, and_6_out, and_7_out, and_8_out, and_9_out, and_11_out, and_10_out, and_12_out, and_14_out);
  not not_21 (not_21_out, in_1[2]);
  not not_22 (not_22_out, in_1[1]);
  not not_23 (not_23_out, in_1[0]);
  and and_9 (and_9_out, not_23_out, not_22_out, not_21_out, in_1[3]);
  not not_24 (not_24_out, in_1[2]);
  not not_25 (not_25_out, in_1[2]);
  not not_26 (not_26_out, in_1[1]);
  not not_27 (not_27_out, in_1[0]);
  and and_10 (and_10_out, not_27_out, in_1[1], not_25_out, in_1[3]);
  and and_11 (and_11_out, in_1[0], not_26_out, not_24_out, in_1[3]);
  or or_4 (l2, and_1_out, and_5_out, and_6_out, and_7_out, and_9_out, and_11_out, and_10_out, and_12_out, and_13_out, and_16_out, and_15_out);
  not not_28 (not_28_out, in_1[2]);
  not not_29 (not_29_out, in_1[1]);
  not not_30 (not_30_out, in_1[0]);
  and and_12 (and_12_out, in_1[0], in_1[1], not_28_out, in_1[3]);
  and and_13 (and_13_out, not_30_out, not_29_out, in_1[2], in_1[3]);
  not not_31 (not_31_out, in_1[1]);
  and and_14 (and_14_out, in_1[0], not_31_out, in_1[2], in_1[3]);
  not not_32 (not_32_out, in_1[0]);
  and and_15 (and_15_out, in_1[0], in_1[1], in_1[2], in_1[3]);
  and and_16 (and_16_out, not_32_out, in_1[1], in_1[2], in_1[3]);
  or or_5 (l4, and_1_out, and_3_out, and_2_out, and_4_out, and_5_out, and_8_out, and_9_out, and_11_out, and_10_out, and_14_out);
  or or_6 (l3, and_1_out, and_2_out, and_4_out, and_6_out, and_8_out, and_9_out, and_7_out, and_11_out, and_10_out, and_13_out, and_16_out, and_15_out);
  or or_7 (l1, and_2_out, and_4_out, and_5_out, and_6_out, and_7_out, and_9_out, and_11_out, and_10_out, and_12_out, and_14_out, and_16_out, and_15_out);
  not not_33 (not_33_out, in_1[7]);
  not not_34 (not_34_out, in_1[6]);
  not not_35 (not_35_out, in_1[5]);
  not not_36 (not_36_out, in_1[4]);
  and and_17 (and_17_out, not_36_out, not_35_out, not_34_out, not_33_out);
  or or_8 (h5, and_17_out, and_18_out, and_23_out, and_25_out, and_27_out, and_28_out, and_30_out, and_29_out, and_31_out, and_32_out);
  not not_37 (not_37_out, in_1[7]);
  not not_38 (not_38_out, in_1[6]);
  not not_39 (not_39_out, in_1[5]);
  not not_40 (not_40_out, in_1[4]);
  and and_18 (and_18_out, not_40_out, in_1[5], not_44_out, not_41_out);
  and and_19 (and_19_out, in_1[4], not_39_out, not_38_out, not_37_out);
  not not_41 (not_41_out, in_1[7]);
  not not_42 (not_42_out, in_1[7]);
  not not_43 (not_43_out, in_1[6]);
  not not_44 (not_44_out, in_1[6]);
  and and_20 (and_20_out, in_1[4], in_1[5], not_43_out, not_42_out);
  not not_45 (not_45_out, in_1[7]);
  not not_46 (not_46_out, in_1[5]);
  not not_47 (not_47_out, in_1[5]);
  not not_48 (not_48_out, in_1[4]);
  and and_21 (and_21_out, in_1[4], not_47_out, in_1[6], not_50_out);
  and and_22 (and_22_out, not_48_out, not_46_out, in_1[6], not_45_out);
  or or_9 (h6, and_17_out, and_18_out, and_20_out, and_21_out, and_23_out, and_25_out, and_28_out, and_30_out, and_29_out, and_31_out);
  not not_49 (not_49_out, in_1[7]);
  not not_50 (not_50_out, in_1[7]);
  not not_51 (not_51_out, in_1[4]);
  and and_23 (and_23_out, not_51_out, in_1[5], in_1[6], not_49_out);
  not not_52 (not_52_out, in_1[7]);
  and and_24 (and_24_out, in_1[4], in_1[5], in_1[6], not_52_out);
  or or_10 (h7, and_17_out, and_19_out, and_20_out, and_22_out, and_21_out, and_23_out, and_24_out, and_25_out, and_26_out, and_27_out, and_28_out, and_29_out);
  not not_53 (not_53_out, in_1[6]);
  not not_54 (not_54_out, in_1[5]);
  not not_55 (not_55_out, in_1[4]);
  and and_25 (and_25_out, not_55_out, not_54_out, not_53_out, in_1[7]);
  not not_56 (not_56_out, in_1[6]);
  not not_57 (not_57_out, in_1[5]);
  not not_58 (not_58_out, in_1[4]);
  and and_26 (and_26_out, in_1[4], not_57_out, not_56_out, in_1[7]);
  and and_27 (and_27_out, not_58_out, in_1[5], not_59_out, in_1[7]);
  not not_59 (not_59_out, in_1[6]);
  not not_60 (not_60_out, in_1[6]);
  and and_28 (and_28_out, in_1[4], in_1[5], not_60_out, in_1[7]);
  or or_11 (h2, and_17_out, and_22_out, and_21_out, and_23_out, and_25_out, and_26_out, and_27_out, and_28_out, and_30_out, and_31_out, and_32_out);
  not not_61 (not_61_out, in_1[5]);
  not not_62 (not_62_out, in_1[5]);
  not not_63 (not_63_out, in_1[4]);
  and and_29 (and_29_out, in_1[4], not_62_out, in_1[6], in_1[7]);
  and and_30 (and_30_out, not_63_out, not_61_out, in_1[6], in_1[7]);
  not not_64 (not_64_out, in_1[4]);
  and and_31 (and_31_out, not_64_out, in_1[5], in_1[6], in_1[7]);
  or or_12 (h4, and_17_out, and_19_out, and_18_out, and_20_out, and_22_out, and_24_out, and_25_out, and_26_out, and_27_out, and_29_out);
  and and_32 (and_32_out, in_1[4], in_1[5], in_1[6], in_1[7]);
  or or_13 (h3, and_17_out, and_18_out, and_20_out, and_21_out, and_24_out, and_25_out, and_23_out, and_26_out, and_27_out, and_30_out, and_31_out, and_32_out);
  or or_14 (h1, and_18_out, and_20_out, and_22_out, and_21_out, and_23_out, and_25_out, and_26_out, and_27_out, and_28_out, and_29_out, and_31_out, and_32_out);
endmodule

module _2_s_complement (
  input  [7:0] INPUT,
  output [7:0] OUTPUT
);

  wire adder_1_cout, adder_2_cout, adder_3_cout, adder_4_cout, adder_5_cout, adder_6_cout, adder_7_cout,
       not_1_out, not_2_out, not_3_out, not_4_out, not_5_out, not_6_out, not_7_out, not_8_out;

  not not_1 (not_1_out, INPUT[0]);
  not not_2 (not_2_out, INPUT[1]);
  not not_3 (not_3_out, INPUT[2]);
  not not_4 (not_4_out, INPUT[3]);
  not not_5 (not_5_out, INPUT[4]);
  not not_6 (not_6_out, INPUT[5]);
  not not_7 (not_7_out, INPUT[6]);
  not not_8 (not_8_out, INPUT[7]);
  Adder #(.width(1)) adder_1 (.a(not_1_out), .b(1'b1), .out(OUTPUT[0]), .cout(adder_1_cout));  // open: cin
  Adder #(.width(1)) adder_2 (.a(not_2_out), .b(adder_1_cout), .out(OUTPUT[1]), .cout(adder_2_cout));  // open: cin
  Adder #(.width(1)) adder_3 (.a(not_3_out), .b(adder_2_cout), .out(OUTPUT[2]), .cout(adder_3_cout));  // open: cin
  Adder #(.width(1)) adder_4 (.a(not_4_out), .b(adder_3_cout), .out(OUTPUT[3]), .cout(adder_4_cout));  // open: cin
  Adder #(.width(1)) adder_5 (.a(not_5_out), .b(adder_4_cout), .out(OUTPUT[4]), .cout(adder_5_cout));  // open: cin
  Adder #(.width(1)) adder_6 (.a(not_6_out), .b(adder_5_cout), .out(OUTPUT[5]), .cout(adder_6_cout));  // open: cin
  Adder #(.width(1)) adder_7 (.a(not_7_out), .b(adder_6_cout), .out(OUTPUT[6]), .cout(adder_7_cout));  // open: cin
  Adder #(.width(1)) adder_8 (.a(not_8_out), .b(adder_7_cout), .out(OUTPUT[7]));  // open: cin, cout
endmodule

module byte_0 (
  input  [2:0] _3A_INPUT,
  input  in_2,
  input  in_3,
  input  in_4,
  input  in_5,
  input  in_6,
  input  in_7,
  input  in_8,
  input  in_9,
  output [7:0] OUTPUT
);

  wire and_1_out, or_1_out, or_2_out, or_3_out, or_4_out, or_5_out, or_6_out, or_7_out, or_8_out;

  buf or_1 (or_1_out, in_2);  // OR_Gate
  or or_2 (or_2_out, in_3, 1'b1);
  buf or_3 (or_3_out, in_4);  // OR_Gate
  buf or_4 (or_4_out, in_5);  // OR_Gate
  or or_5 (or_5_out, in_6, 1'b1);
  or or_6 (or_6_out, in_7, 1'b1);
  or or_7 (or_7_out, in_8, 1'b1);
  or or_8 (or_8_out, in_9, 1'b1);
  and and_1 (and_1_out, _3A_INPUT[0], _3A_INPUT[1], _3A_INPUT[2]);
  D_Flip_Flop d_ff_1 (.clk(and_1_out), .D(or_1_out), .Q(OUTPUT[7]));  // open: Qn, preset, en, reset
  D_Flip_Flop d_ff_2 (.clk(and_1_out), .D(or_2_out), .Q(OUTPUT[6]));  // open: Qn, preset, en, reset
  D_Flip_Flop d_ff_3 (.clk(and_1_out), .D(or_3_out), .Q(OUTPUT[5]));  // open: Qn, preset, en, reset
  D_Flip_Flop d_ff_4 (.clk(and_1_out), .D(or_4_out), .Q(OUTPUT[4]));  // open: Qn, preset, en, reset
  D_Flip_Flop d_ff_5 (.clk(and_1_out), .D(or_5_out), .Q(OUTPUT[3]));  // open: Qn, preset, en, reset
  D_Flip_Flop d_ff_6 (.clk(and_1_out), .D(or_6_out), .Q(OUTPUT[2]));  // open: Qn, preset, en, reset
  D_Flip_Flop d_ff_7 (.clk(and_1_out), .D(or_7_out), .Q(OUTPUT[1]));  // open: Qn, preset, en, reset
  D_Flip_Flop d_ff_8 (.clk(and_1_out), .D(or_8_out), .Q(OUTPUT[0]));  // open: Qn, preset, en, reset
endmodule

module byte1 (
  input  [2:0] _3A_INPUT,
  input  in_2,
  input  in_3,
  input  in_4,
  input  in_5,
  input  in_6,
  input  in_7,
  input  in_8,
  input  in_9,
  output [7:0] OUTPUT
);

  wire and_1_out, or_1_out, or_2_out, or_3_out, or_4_out, or_5_out, or_6_out, or_7_out, or_8_out;

  or or_1 (or_1_out, in_2, 1'b1);
  buf or_2 (or_2_out, in_3);  // OR_Gate
  or or_3 (or_3_out, in_4, 1'b1);
  or or_4 (or_4_out, in_5, 1'b1);
  buf or_5 (or_5_out, in_6);  // OR_Gate
  buf or_6 (or_6_out, in_7);  // OR_Gate
  buf or_7 (or_7_out, in_8);  // OR_Gate
  buf or_8 (or_8_out, in_9);  // OR_Gate
  and and_1 (and_1_out, _3A_INPUT[0], _3A_INPUT[1], _3A_INPUT[2]);
  D_Flip_Flop d_ff_1 (.clk(and_1_out), .D(or_1_out), .Q(OUTPUT[7]));  // open: Qn, preset, en, reset
  D_Flip_Flop d_ff_2 (.clk(and_1_out), .D(or_2_out), .Q(OUTPUT[6]));  // open: Qn, preset, en, reset
  D_Flip_Flop d_ff_3 (.clk(and_1_out), .D(or_3_out), .Q(OUTPUT[5]));  // open: Qn, preset, en, reset
  D_Flip_Flop d_ff_4 (.clk(and_1_out), .D(or_4_out), .Q(OUTPUT[4]));  // open: Qn, preset, en, reset
  D_Flip_Flop d_ff_5 (.clk(and_1_out), .D(or_5_out), .Q(OUTPUT[3]));  // open: Qn, preset, en, reset
  D_Flip_Flop d_ff_6 (.clk(and_1_out), .D(or_6_out), .Q(OUTPUT[2]));  // open: Qn, preset, en, reset
  D_Flip_Flop d_ff_7 (.clk(and_1_out), .D(or_7_out), .Q(OUTPUT[1]));  // open: Qn, preset, en, reset
  D_Flip_Flop d_ff_8 (.clk(and_1_out), .D(or_8_out), .Q(OUTPUT[0]));  // open: Qn, preset, en, reset
endmodule

module byte2 (
  input  [2:0] _3A_INPUT,
  input  in_2,
  input  in_3,
  input  in_4,
  input  in_5,
  input  in_6,
  input  in_7,
  input  in_8,
  input  in_9,
  output [7:0] OUTPUT
);

  wire and_1_out, or_1_out, or_2_out, or_3_out, or_4_out, or_5_out, or_6_out, or_7_out, or_8_out;

  buf or_1 (or_1_out, in_2);  // OR_Gate
  buf or_2 (or_2_out, in_3);  // OR_Gate
  buf or_3 (or_3_out, in_4);  // OR_Gate
  buf or_4 (or_4_out, in_5);  // OR_Gate
  buf or_5 (or_5_out, in_6);  // OR_Gate
  buf or_6 (or_6_out, in_7);  // OR_Gate
  buf or_7 (or_7_out, in_8);  // OR_Gate
  or or_8 (or_8_out, in_9, 1'b1);
  and and_1 (and_1_out, _3A_INPUT[0], _3A_INPUT[1], _3A_INPUT[2]);
  D_Flip_Flop d_ff_1 (.clk(and_1_out), .D(or_1_out), .Q(OUTPUT[7]));  // open: Qn, preset, en, reset
  D_Flip_Flop d_ff_2 (.clk(and_1_out), .D(or_2_out), .Q(OUTPUT[6]));  // open: Qn, preset, en, reset
  D_Flip_Flop d_ff_3 (.clk(and_1_out), .D(or_3_out), .Q(OUTPUT[5]));  // open: Qn, preset, en, reset
  D_Flip_Flop d_ff_4 (.clk(and_1_out), .D(or_4_out), .Q(OUTPUT[4]));  // open: Qn, preset, en, reset
  D_Flip_Flop d_ff_5 (.clk(and_1_out), .D(or_5_out), .Q(OUTPUT[3]));  // open: Qn, preset, en, reset
  D_Flip_Flop d_ff_6 (.clk(and_1_out), .D(or_6_out), .Q(OUTPUT[2]));  // open: Qn, preset, en, reset
  D_Flip_Flop d_ff_7 (.clk(and_1_out), .D(or_7_out), .Q(OUTPUT[1]));  // open: Qn, preset, en, reset
  D_Flip_Flop d_ff_8 (.clk(and_1_out), .D(or_8_out), .Q(OUTPUT[0]));  // open: Qn, preset, en, reset
endmodule

module byte3 (
  input  [2:0] _3A_INPUT,
  input  in_2,
  input  in_3,
  input  in_4,
  input  in_5,
  input  in_6,
  input  in_7,
  input  in_8,
  input  in_9,
  output [7:0] OUTPUT
);

  wire and_1_out, or_1_out, or_2_out, or_3_out, or_4_out, or_5_out, or_6_out, or_7_out, or_8_out;

  buf or_1 (or_1_out, in_2);  // OR_Gate
  buf or_2 (or_2_out, in_3);  // OR_Gate
  or or_3 (or_3_out, in_4, 1'b1);
  buf or_4 (or_4_out, in_5);  // OR_Gate
  or or_5 (or_5_out, in_6, 1'b1);
  or or_6 (or_6_out, in_7, 1'b1);
  or or_7 (or_7_out, in_8, 1'b1);
  or or_8 (or_8_out, in_9, 1'b1);
  and and_1 (and_1_out, _3A_INPUT[0], _3A_INPUT[1], _3A_INPUT[2]);
  D_Flip_Flop d_ff_1 (.clk(and_1_out), .D(or_1_out), .Q(OUTPUT[7]));  // open: Qn, preset, en, reset
  D_Flip_Flop d_ff_2 (.clk(and_1_out), .D(or_2_out), .Q(OUTPUT[6]));  // open: Qn, preset, en, reset
  D_Flip_Flop d_ff_3 (.clk(and_1_out), .D(or_3_out), .Q(OUTPUT[5]));  // open: Qn, preset, en, reset
  D_Flip_Flop d_ff_4 (.clk(and_1_out), .D(or_4_out), .Q(OUTPUT[4]));  // open: Qn, preset, en, reset
  D_Flip_Flop d_ff_5 (.clk(and_1_out), .D(or_5_out), .Q(OUTPUT[3]));  // open: Qn, preset, en, reset
  D_Flip_Flop d_ff_6 (.clk(and_1_out), .D(or_6_out), .Q(OUTPUT[2]));  // open: Qn, preset, en, reset
  D_Flip_Flop d_ff_7 (.clk(and_1_out), .D(or_7_out), .Q(OUTPUT[1]));  // open: Qn, preset, en, reset
  D_Flip_Flop d_ff_8 (.clk(and_1_out), .D(or_8_out), .Q(OUTPUT[0]));  // open: Qn, preset, en, reset
endmodule

module byte4 (
  input  [2:0] _3A_INPUT,
  input  in_2,
  input  in_3,
  input  in_4,
  input  in_5,
  input  in_6,
  input  in_7,
  input  in_8,
  input  in_9,
  output [7:0] OUTPUT
);

  wire and_1_out, or_1_out, or_2_out, or_3_out, or_4_out, or_5_out, or_6_out, or_7_out, or_8_out;

  buf or_1 (or_1_out, in_2);  // OR_Gate
  or or_2 (or_2_out, in_3, 1'b1);
  buf or_3 (or_3_out, in_4);  // OR_Gate
  or or_4 (or_4_out, in_5, 1'b1);
  buf or_5 (or_5_out, in_6);  // OR_Gate
  buf or_6 (or_6_out, in_7);  // OR_Gate
  or or_7 (or_7_out, in_8, 1'b1);
  buf or_8 (or_8_out, in_9);  // OR_Gate
  and and_1 (and_1_out, _3A_INPUT[0], _3A_INPUT[1], _3A_INPUT[2]);
  D_Flip_Flop d_ff_1 (.clk(and_1_out), .D(or_1_out), .Q(OUTPUT[7]));  // open: Qn, preset, en, reset
  D_Flip_Flop d_ff_2 (.clk(and_1_out), .D(or_2_out), .Q(OUTPUT[6]));  // open: Qn, preset, en, reset
  D_Flip_Flop d_ff_3 (.clk(and_1_out), .D(or_3_out), .Q(OUTPUT[5]));  // open: Qn, preset, en, reset
  D_Flip_Flop d_ff_4 (.clk(and_1_out), .D(or_4_out), .Q(OUTPUT[4]));  // open: Qn, preset, en, reset
  D_Flip_Flop d_ff_5 (.clk(and_1_out), .D(or_5_out), .Q(OUTPUT[3]));  // open: Qn, preset, en, reset
  D_Flip_Flop d_ff_6 (.clk(and_1_out), .D(or_6_out), .Q(OUTPUT[2]));  // open: Qn, preset, en, reset
  D_Flip_Flop d_ff_7 (.clk(and_1_out), .D(or_7_out), .Q(OUTPUT[1]));  // open: Qn, preset, en, reset
  D_Flip_Flop d_ff_8 (.clk(and_1_out), .D(or_8_out), .Q(OUTPUT[0]));  // open: Qn, preset, en, reset
endmodule

module byte5 (
  input  [2:0] _3A_INPUT,
  input  in_2,
  input  in_3,
  input  in_4,
  input  in_5,
  input  in_6,
  input  in_7,
  input  in_8,
  input  in_9,
  output [7:0] OUTPUT
);

  wire and_1_out, or_1_out, or_2_out, or_3_out, or_4_out, or_5_out, or_6_out, or_7_out, or_8_out;

  buf or_1 (or_1_out, in_2);  // OR_Gate
  or or_2 (or_2_out, in_3, 1'b1);
  buf or_3 (or_3_out, in_4);  // OR_Gate
  buf or_4 (or_4_out, in_5);  // OR_Gate
  or or_5 (or_5_out, in_6, 1'b1);
  or or_6 (or_6_out, in_7, 1'b1);
  or or_7 (or_7_out, in_8, 1'b1);
  buf or_8 (or_8_out, in_9);  // OR_Gate
  and and_1 (and_1_out, _3A_INPUT[0], _3A_INPUT[1], _3A_INPUT[2]);
  D_Flip_Flop d_ff_1 (.clk(and_1_out), .D(or_1_out), .Q(OUTPUT[7]));  // open: Qn, preset, en, reset
  D_Flip_Flop d_ff_2 (.clk(and_1_out), .D(or_2_out), .Q(OUTPUT[6]));  // open: Qn, preset, en, reset
  D_Flip_Flop d_ff_3 (.clk(and_1_out), .D(or_3_out), .Q(OUTPUT[5]));  // open: Qn, preset, en, reset
  D_Flip_Flop d_ff_4 (.clk(and_1_out), .D(or_4_out), .Q(OUTPUT[4]));  // open: Qn, preset, en, reset
  D_Flip_Flop d_ff_5 (.clk(and_1_out), .D(or_5_out), .Q(OUTPUT[3]));  // open: Qn, preset, en, reset
  D_Flip_Flop d_ff_6 (.clk(and_1_out), .D(or_6_out), .Q(OUTPUT[2]));  // open: Qn, preset, en, reset
  D_Flip_Flop d_ff_7 (.clk(and_1_out), .D(or_7_out), .Q(OUTPUT[1]));  // open: Qn, preset, en, reset
  D_Flip_Flop d_ff_8 (.clk(and_1_out), .D(or_8_out), .Q(OUTPUT[0]));  // open: Qn, preset, en, reset
endmodule

module byte6 (
  input  [2:0] _3A_INPUT,
  input  in_2,
  input  in_3,
  input  in_4,
  input  in_5,
  input  in_6,
  input  in_7,
  input  in_8,
  input  in_9,
  output [7:0] OUTPUT
);

  wire and_1_out, or_1_out, or_2_out, or_3_out, or_4_out, or_5_out, or_6_out, or_7_out, or_8_out;

  buf or_1 (or_1_out, in_2);  // OR_Gate
  or or_2 (or_2_out, in_3, 1'b1);
  or or_3 (or_3_out, in_4, 1'b1);
  buf or_4 (or_4_out, in_5);  // OR_Gate
  or or_5 (or_5_out, in_6, 1'b1);
  buf or_6 (or_6_out, in_7);  // OR_Gate
  or or_7 (or_7_out, in_8, 1'b1);
  or or_8 (or_8_out, in_9, 1'b1);
  and and_1 (and_1_out, _3A_INPUT[0], _3A_INPUT[1], _3A_INPUT[2]);
  D_Flip_Flop d_ff_1 (.clk(and_1_out), .D(or_1_out), .Q(OUTPUT[7]));  // open: Qn, preset, en, reset
  D_Flip_Flop d_ff_2 (.clk(and_1_out), .D(or_2_out), .Q(OUTPUT[6]));  // open: Qn, preset, en, reset
  D_Flip_Flop d_ff_3 (.clk(and_1_out), .D(or_3_out), .Q(OUTPUT[5]));  // open: Qn, preset, en, reset
  D_Flip_Flop d_ff_4 (.clk(and_1_out), .D(or_4_out), .Q(OUTPUT[4]));  // open: Qn, preset, en, reset
  D_Flip_Flop d_ff_5 (.clk(and_1_out), .D(or_5_out), .Q(OUTPUT[3]));  // open: Qn, preset, en, reset
  D_Flip_Flop d_ff_6 (.clk(and_1_out), .D(or_6_out), .Q(OUTPUT[2]));  // open: Qn, preset, en, reset
  D_Flip_Flop d_ff_7 (.clk(and_1_out), .D(or_7_out), .Q(OUTPUT[1]));  // open: Qn, preset, en, reset
  D_Flip_Flop d_ff_8 (.clk(and_1_out), .D(or_8_out), .Q(OUTPUT[0]));  // open: Qn, preset, en, reset
endmodule

module byte7 (
  input  [2:0] _3A_INPUT,
  input  in_2,
  input  in_3,
  input  in_4,
  input  in_5,
  input  in_6,
  input  in_7,
  input  in_8,
  input  in_9,
  output [7:0] OUTPUT
);

  wire and_1_out, or_1_out, or_2_out, or_3_out, or_4_out, or_5_out, or_6_out, or_7_out, or_8_out;

  or or_1 (or_1_out, in_2, 1'b1);
  or or_2 (or_2_out, in_3, 1'b1);
  buf or_3 (or_3_out, in_4);  // OR_Gate
  buf or_4 (or_4_out, in_5);  // OR_Gate
  buf or_5 (or_5_out, in_6);  // OR_Gate
  buf or_6 (or_6_out, in_7);  // OR_Gate
  buf or_7 (or_7_out, in_8);  // OR_Gate
  buf or_8 (or_8_out, in_9);  // OR_Gate
  and and_1 (and_1_out, _3A_INPUT[0], _3A_INPUT[1], _3A_INPUT[2]);
  D_Flip_Flop d_ff_1 (.clk(and_1_out), .D(or_1_out), .Q(OUTPUT[7]));  // open: Qn, preset, en, reset
  D_Flip_Flop d_ff_2 (.clk(and_1_out), .D(or_2_out), .Q(OUTPUT[6]));  // open: Qn, preset, en, reset
  D_Flip_Flop d_ff_3 (.clk(and_1_out), .D(or_3_out), .Q(OUTPUT[5]));  // open: Qn, preset, en, reset
  D_Flip_Flop d_ff_4 (.clk(and_1_out), .D(or_4_out), .Q(OUTPUT[4]));  // open: Qn, preset, en, reset
  D_Flip_Flop d_ff_5 (.clk(and_1_out), .D(or_5_out), .Q(OUTPUT[3]));  // open: Qn, preset, en, reset
  D_Flip_Flop d_ff_6 (.clk(and_1_out), .D(or_6_out), .Q(OUTPUT[2]));  // open: Qn, preset, en, reset
  D_Flip_Flop d_ff_7 (.clk(and_1_out), .D(or_7_out), .Q(OUTPUT[1]));  // open: Qn, preset, en, reset
  D_Flip_Flop d_ff_8 (.clk(and_1_out), .D(or_8_out), .Q(OUTPUT[0]));  // open: Qn, preset, en, reset
endmodule

module byte8 (
  input  [2:0] _3A_INPUT,
  input  in_2,
  input  in_3,
  input  in_4,
  input  in_5,
  input  in_6,
  input  in_7,
  input  in_8,
  input  in_9,
  output [7:0] OUTPUT
);

  wire and_1_out, or_1_out, or_2_out, or_3_out, or_4_out, or_5_out, or_6_out, or_7_out, or_8_out;

  buf or_1 (or_1_out, in_2);  // OR_Gate
  buf or_2 (or_2_out, in_3);  // OR_Gate
  or or_3 (or_3_out, in_4, 1'b1);
  buf or_4 (or_4_out, in_5);  // OR_Gate
  or or_5 (or_5_out, in_6, 1'b1);
  or or_6 (or_6_out, in_7, 1'b1);
  or or_7 (or_7_out, in_8, 1'b1);
  buf or_8 (or_8_out, in_9);  // OR_Gate
  and and_1 (and_1_out, _3A_INPUT[0], _3A_INPUT[1], _3A_INPUT[2]);
  D_Flip_Flop d_ff_1 (.clk(and_1_out), .D(or_1_out), .Q(OUTPUT[7]));  // open: Qn, preset, en, reset
  D_Flip_Flop d_ff_2 (.clk(and_1_out), .D(or_2_out), .Q(OUTPUT[6]));  // open: Qn, preset, en, reset
  D_Flip_Flop d_ff_3 (.clk(and_1_out), .D(or_3_out), .Q(OUTPUT[5]));  // open: Qn, preset, en, reset
  D_Flip_Flop d_ff_4 (.clk(and_1_out), .D(or_4_out), .Q(OUTPUT[4]));  // open: Qn, preset, en, reset
  D_Flip_Flop d_ff_5 (.clk(and_1_out), .D(or_5_out), .Q(OUTPUT[3]));  // open: Qn, preset, en, reset
  D_Flip_Flop d_ff_6 (.clk(and_1_out), .D(or_6_out), .Q(OUTPUT[2]));  // open: Qn, preset, en, reset
  D_Flip_Flop d_ff_7 (.clk(and_1_out), .D(or_7_out), .Q(OUTPUT[1]));  // open: Qn, preset, en, reset
  D_Flip_Flop d_ff_8 (.clk(and_1_out), .D(or_8_out), .Q(OUTPUT[0]));  // open: Qn, preset, en, reset
endmodule

module byte9 (
  input  [2:0] _3A_INPUT,
  input  in_2,
  input  in_3,
  input  in_4,
  input  in_5,
  input  in_6,
  input  in_7,
  input  in_8,
  input  in_9,
  output [7:0] OUTPUT
);

  wire and_1_out, or_1_out, or_2_out, or_3_out, or_4_out, or_5_out, or_6_out, or_7_out, or_8_out;

  buf or_1 (or_1_out, in_2);  // OR_Gate
  or or_2 (or_2_out, in_3, 1'b1);
  buf or_3 (or_3_out, in_4);  // OR_Gate
  buf or_4 (or_4_out, in_5);  // OR_Gate
  buf or_5 (or_5_out, in_6);  // OR_Gate
  buf or_6 (or_6_out, in_7);  // OR_Gate
  or or_7 (or_7_out, in_8, 1'b1);
  buf or_8 (or_8_out, in_9);  // OR_Gate
  and and_1 (and_1_out, _3A_INPUT[0], _3A_INPUT[1], _3A_INPUT[2]);
  D_Flip_Flop d_ff_1 (.clk(and_1_out), .D(or_1_out), .Q(OUTPUT[7]));  // open: Qn, preset, en, reset
  D_Flip_Flop d_ff_2 (.clk(and_1_out), .D(or_2_out), .Q(OUTPUT[6]));  // open: Qn, preset, en, reset
  D_Flip_Flop d_ff_3 (.clk(and_1_out), .D(or_3_out), .Q(OUTPUT[5]));  // open: Qn, preset, en, reset
  D_Flip_Flop d_ff_4 (.clk(and_1_out), .D(or_4_out), .Q(OUTPUT[4]));  // open: Qn, preset, en, reset
  D_Flip_Flop d_ff_5 (.clk(and_1_out), .D(or_5_out), .Q(OUTPUT[3]));  // open: Qn, preset, en, reset
  D_Flip_Flop d_ff_6 (.clk(and_1_out), .D(or_6_out), .Q(OUTPUT[2]));  // open: Qn, preset, en, reset
  D_Flip_Flop d_ff_7 (.clk(and_1_out), .D(or_7_out), .Q(OUTPUT[1]));  // open: Qn, preset, en, reset
  D_Flip_Flop d_ff_8 (.clk(and_1_out), .D(or_8_out), .Q(OUTPUT[0]));  // open: Qn, preset, en, reset
endmodule

module byte10 (
  input  [2:0] _3A_INPUT,
  input  in_2,
  input  in_3,
  input  in_4,
  input  in_5,
  input  in_6,
  input  in_7,
  input  in_8,
  input  in_9,
  output [7:0] OUTPUT
);

  wire and_1_out, or_1_out, or_2_out, or_3_out, or_4_out, or_5_out, or_6_out, or_7_out, or_8_out;

  buf or_1 (or_1_out, in_2);  // OR_Gate
  or or_2 (or_2_out, in_3, 1'b1);
  or or_3 (or_3_out, in_4, 1'b1);
  buf or_4 (or_4_out, in_5);  // OR_Gate
  buf or_5 (or_5_out, in_6);  // OR_Gate
  buf or_6 (or_6_out, in_7);  // OR_Gate
  buf or_7 (or_7_out, in_8);  // OR_Gate
  buf or_8 (or_8_out, in_9);  // OR_Gate
  and and_1 (and_1_out, _3A_INPUT[0], _3A_INPUT[1], _3A_INPUT[2]);
  D_Flip_Flop d_ff_1 (.clk(and_1_out), .D(or_1_out), .Q(OUTPUT[7]));  // open: Qn, preset, en, reset
  D_Flip_Flop d_ff_2 (.clk(and_1_out), .D(or_2_out), .Q(OUTPUT[6]));  // open: Qn, preset, en, reset
  D_Flip_Flop d_ff_3 (.clk(and_1_out), .D(or_3_out), .Q(OUTPUT[5]));  // open: Qn, preset, en, reset
  D_Flip_Flop d_ff_4 (.clk(and_1_out), .D(or_4_out), .Q(OUTPUT[4]));  // open: Qn, preset, en, reset
  D_Flip_Flop d_ff_5 (.clk(and_1_out), .D(or_5_out), .Q(OUTPUT[3]));  // open: Qn, preset, en, reset
  D_Flip_Flop d_ff_6 (.clk(and_1_out), .D(or_6_out), .Q(OUTPUT[2]));  // open: Qn, preset, en, reset
  D_Flip_Flop d_ff_7 (.clk(and_1_out), .D(or_7_out), .Q(OUTPUT[1]));  // open: Qn, preset, en, reset
  D_Flip_Flop d_ff_8 (.clk(and_1_out), .D(or_8_out), .Q(OUTPUT[0]));  // open: Qn, preset, en, reset
endmodule

module byte11 (
  input  [2:0] _3A_INPUT,
  input  in_2,
  input  in_3,
  input  in_4,
  input  in_5,
  input  in_6,
  input  in_7,
  input  in_8,
  input  in_9,
  output [7:0] OUTPUT
);

  wire and_1_out, or_1_out, or_2_out, or_3_out, or_4_out, or_5_out, or_6_out, or_7_out, or_8_out;

  buf or_1 (or_1_out, in_2);  // OR_Gate
  or or_2 (or_2_out, in_3, 1'b1);
  buf or_3 (or_3_out, in_4);  // OR_Gate
  buf or_4 (or_4_out, in_5);  // OR_Gate
  or or_5 (or_5_out, in_6, 1'b1);
  or or_6 (or_6_out, in_7, 1'b1);
  or or_7 (or_7_out, in_8, 1'b1);
  or or_8 (or_8_out, in_9, 1'b1);
  and and_1 (and_1_out, _3A_INPUT[0], _3A_INPUT[1], _3A_INPUT[2]);
  D_Flip_Flop d_ff_1 (.clk(and_1_out), .D(or_1_out), .Q(OUTPUT[7]));  // open: Qn, preset, en, reset
  D_Flip_Flop d_ff_2 (.clk(and_1_out), .D(or_2_out), .Q(OUTPUT[6]));  // open: Qn, preset, en, reset
  D_Flip_Flop d_ff_3 (.clk(and_1_out), .D(or_3_out), .Q(OUTPUT[5]));  // open: Qn, preset, en, reset
  D_Flip_Flop d_ff_4 (.clk(and_1_out), .D(or_4_out), .Q(OUTPUT[4]));  // open: Qn, preset, en, reset
  D_Flip_Flop d_ff_5 (.clk(and_1_out), .D(or_5_out), .Q(OUTPUT[3]));  // open: Qn, preset, en, reset
  D_Flip_Flop d_ff_6 (.clk(and_1_out), .D(or_6_out), .Q(OUTPUT[2]));  // open: Qn, preset, en, reset
  D_Flip_Flop d_ff_7 (.clk(and_1_out), .D(or_7_out), .Q(OUTPUT[1]));  // open: Qn, preset, en, reset
  D_Flip_Flop d_ff_8 (.clk(and_1_out), .D(or_8_out), .Q(OUTPUT[0]));  // open: Qn, preset, en, reset
endmodule

module byte12 (
  input  [2:0] _3A_INPUT,
  input  in_2,
  input  in_3,
  input  in_4,
  input  in_5,
  input  in_6,
  input  in_7,
  input  in_8,
  input  in_9,
  output [7:0] OUTPUT
);

  wire and_1_out, or_1_out, or_2_out, or_3_out, or_4_out, or_5_out, or_6_out, or_7_out, or_8_out;

  or or_1 (or_1_out, in_2, 1'b1);
  buf or_2 (or_2_out, in_3);  // OR_Gate
  buf or_3 (or_3_out, in_4);  // OR_Gate
  buf or_4 (or_4_out, in_5);  // OR_Gate
  buf or_5 (or_5_out, in_6);  // OR_Gate
  buf or_6 (or_6_out, in_7);  // OR_Gate
  buf or_7 (or_7_out, in_8);  // OR_Gate
  buf or_8 (or_8_out, in_9);  // OR_Gate
  and and_1 (and_1_out, _3A_INPUT[0], _3A_INPUT[1], _3A_INPUT[2]);
  D_Flip_Flop d_ff_1 (.clk(and_1_out), .D(or_1_out), .Q(OUTPUT[7]));  // open: Qn, preset, en, reset
  D_Flip_Flop d_ff_2 (.clk(and_1_out), .D(or_2_out), .Q(OUTPUT[6]));  // open: Qn, preset, en, reset
  D_Flip_Flop d_ff_3 (.clk(and_1_out), .D(or_3_out), .Q(OUTPUT[5]));  // open: Qn, preset, en, reset
  D_Flip_Flop d_ff_4 (.clk(and_1_out), .D(or_4_out), .Q(OUTPUT[4]));  // open: Qn, preset, en, reset
  D_Flip_Flop d_ff_5 (.clk(and_1_out), .D(or_5_out), .Q(OUTPUT[3]));  // open: Qn, preset, en, reset
  D_Flip_Flop d_ff_6 (.clk(and_1_out), .D(or_6_out), .Q(OUTPUT[2]));  // open: Qn, preset, en, reset
  D_Flip_Flop d_ff_7 (.clk(and_1_out), .D(or_7_out), .Q(OUTPUT[1]));  // open: Qn, preset, en, reset
  D_Flip_Flop d_ff_8 (.clk(and_1_out), .D(or_8_out), .Q(OUTPUT[0]));  // open: Qn, preset, en, reset
endmodule

module byte13 (
  input  [2:0] _3A_INPUT,
  input  in_2,
  input  in_3,
  input  in_4,
  input  in_5,
  input  in_6,
  input  in_7,
  input  in_8,
  input  in_9,
  output [7:0] OUTPUT
);

  wire and_1_out, or_1_out, or_2_out, or_3_out, or_4_out, or_5_out, or_6_out, or_7_out, or_8_out;

  buf or_1 (or_1_out, in_2);  // OR_Gate
  or or_2 (or_2_out, in_3, 1'b1);
  or or_3 (or_3_out, in_4, 1'b1);
  or or_4 (or_4_out, in_5, 1'b1);
  buf or_5 (or_5_out, in_6);  // OR_Gate
  buf or_6 (or_6_out, in_7);  // OR_Gate
  buf or_7 (or_7_out, in_8);  // OR_Gate
  buf or_8 (or_8_out, in_9);  // OR_Gate
  and and_1 (and_1_out, _3A_INPUT[0], _3A_INPUT[1], _3A_INPUT[2]);
  D_Flip_Flop d_ff_1 (.clk(and_1_out), .D(or_1_out), .Q(OUTPUT[7]));  // open: Qn, preset, en, reset
  D_Flip_Flop d_ff_2 (.clk(and_1_out), .D(or_2_out), .Q(OUTPUT[6]));  // open: Qn, preset, en, reset
  D_Flip_Flop d_ff_3 (.clk(and_1_out), .D(or_3_out), .Q(OUTPUT[5]));  // open: Qn, preset, en, reset
  D_Flip_Flop d_ff_4 (.clk(and_1_out), .D(or_4_out), .Q(OUTPUT[4]));  // open: Qn, preset, en, reset
  D_Flip_Flop d_ff_5 (.clk(and_1_out), .D(or_5_out), .Q(OUTPUT[3]));  // open: Qn, preset, en, reset
  D_Flip_Flop d_ff_6 (.clk(and_1_out), .D(or_6_out), .Q(OUTPUT[2]));  // open: Qn, preset, en, reset
  D_Flip_Flop d_ff_7 (.clk(and_1_out), .D(or_7_out), .Q(OUTPUT[1]));  // open: Qn, preset, en, reset
  D_Flip_Flop d_ff_8 (.clk(and_1_out), .D(or_8_out), .Q(OUTPUT[0]));  // open: Qn, preset, en, reset
endmodule
